// Logisim project 11-Extensor_sinal_4_8.circ as structural Verilog: 1 circuit, main circuit EXT_SINAL_4_8
module EXT_SINAL_4_8 (
  input  A3,
  input  A2,
  input  A1,
  input  A0,
  output [7:0] EXT
);


  assign EXT = {{5{A3}}, A2, A1, A0};

  // Notes on the sheet:
  //   A3 = bit de sinal: copiado para os bits 3 a 7 (sem portas logicas)
endmodule
