// Logisim project 14-ParidadeImpar.circ as structural Verilog: 1 circuit, main circuit main
module main (
  input  in_1,
  input  in_2,
  input  in_3,
  input  in_4,
  input  in_5,
  input  in_6,
  input  in_7,
  input  in_8,
  output out_9
);

  wire xor_1_out, xor_2_out, xor_3_out, xor_4_out, xor_5_out, xor_6_out;

  xor xor_1 (xor_1_out, in_1, in_2);
  xor xor_2 (xor_2_out, xor_1_out, in_3);
  xor xor_3 (xor_3_out, xor_2_out, in_4);
  xor xor_4 (xor_4_out, xor_3_out, in_5);
  xor xor_5 (xor_5_out, xor_4_out, in_6);
  xor xor_6 (xor_6_out, xor_5_out, in_7);
  xor xor_7 (out_9, xor_6_out, in_8);
endmodule
