// Logisim project 16-DEC_7SEG.circ as structural Verilog: 1 circuit, main circuit DEC_7SEG
module DEC_7SEG (
  input  A,
  input  B,
  input  C,
  input  D
);

  wire and_1_out, and_2_out, and_3_out, and_4_out, and_5_out, and_6_out, and_7_out, and_8_out, and_9_out,
       not_1_out, not_2_out, not_3_out, or_1_out, or_2_out, or_3_out, or_4_out, or_5_out, or_6_out, or_7_out;

  not not_1 (not_1_out, B);
  not not_2 (not_2_out, C);
  not not_3 (not_3_out, D);
  and and_1 (and_1_out, B, D);
  and and_2 (and_2_out, not_1_out, not_3_out);
  and and_3 (and_3_out, not_2_out, not_3_out);
  and and_4 (and_4_out, C, D);
  and and_5 (and_5_out, not_1_out, C);
  and and_6 (and_6_out, C, not_3_out);
  and and_7 (and_7_out, B, not_2_out, D);
  and and_8 (and_8_out, B, not_2_out);
  and and_9 (and_9_out, B, not_3_out);
  or or_1 (or_1_out, A, C, and_1_out, and_2_out);
  or or_2 (or_2_out, not_1_out, and_3_out, and_4_out);
  or or_3 (or_3_out, B, not_2_out, D);
  or or_4 (or_4_out, A, and_2_out, and_5_out, and_6_out, and_7_out);
  or or_5 (or_5_out, and_2_out, and_6_out);
  or or_6 (or_6_out, A, and_3_out, and_8_out, and_9_out);
  or or_7 (or_7_out, A, and_5_out, and_8_out, and_6_out);
  _7_Segment_Display u_7_segment_display_1 (
    .g(or_7_out), .f(or_6_out), .a(or_1_out), .b(or_2_out), .e(or_5_out), .d(or_4_out), .c(or_3_out));  // open: dp

  // Notes on the sheet:
  //   DEC_7SEG: entrada ABCD (A = MSB), saidas a..g ativas em 1 (0 a 9; 10-15 indiferentes)
endmodule
