// Logisim project 17-PRIMO4.circ as structural Verilog: 1 circuit, main circuit PRIMO4
module PRIMO4 (
  input  A,
  input  B,
  input  C,
  input  D,
  output P
);

  wire and_1_out, and_2_out, and_3_out, and_4_out, not_1_out, not_2_out, not_3_out;

  not not_1 (not_1_out, A);
  not not_2 (not_2_out, B);
  not not_3 (not_3_out, C);
  and and_1 (and_1_out, not_1_out, not_2_out, C);
  and and_2 (and_2_out, not_1_out, B, D);
  and and_3 (and_3_out, not_2_out, C, D);
  and and_4 (and_4_out, B, not_3_out, D);
  or or_1 (P, and_1_out, and_2_out, and_3_out, and_4_out);

  // Notes on the sheet:
  //   PRIMO4: P = A'B'C + A'BD + B'CD + BC'D  (primos: 2, 3, 5, 7, 11, 13)
  //   A' 
  //   B
  //   B'
  //   C
  //   C'
  //   D
endmodule
