// Logisim project parte1_cache.circ as structural Verilog: 16 circuits, main circuit CACHE_PARTE1
module xor2 (
  input  x,
  input  Y,
  output S
);

  wire and_1_out, and_2_out, not_1_out, not_2_out;

  not not_1 (not_1_out, x);
  not not_2 (not_2_out, Y);
  and and_1 (and_1_out, x, not_2_out);
  and and_2 (and_2_out, not_1_out, Y);
  or or_1 (S, and_1_out, and_2_out);

  // Notes on the sheet:
  //   LEGENDA: xor2 = XOR feito com AND, OR e NOT (Componente 03)
  //   S = x.Y' + x'.Y  ->  S=1 quando as entradas sao DIFERENTES
endmodule

module Primo4 (
  input  A,
  input  B,
  input  C,
  input  D,
  output P
);

  wire and_1_out, and_2_out, and_3_out, and_4_out, not_1_out, not_2_out, not_3_out;

  not not_1 (not_1_out, A);
  not not_2 (not_2_out, B);
  not not_3 (not_3_out, C);
  and and_1 (and_1_out, not_1_out, not_2_out, C);
  and and_2 (and_2_out, not_1_out, B, D);
  and and_3 (and_3_out, not_2_out, C, D);
  and and_4 (and_4_out, B, not_3_out, D);
  or or_1 (P, and_1_out, and_2_out, and_3_out, and_4_out);

  // Notes on the sheet:
  //   LEGENDA: Primo4 = Detector de numero primo de 4 bits (Componente 17)
  //   A B C D = numero de 4 bits (A = bit mais alto)
  //   P = 1 se o numero e primo (2, 3, 5, 7, 11, 13)
endmodule

module MUX4_8 (
  input  [7:0] I0,
  input  [7:0] I1,
  input  [7:0] I2,
  input  [7:0] I3,
  input  S1,
  input  S0,
  output [7:0] Y
);

  wire not_1_out, not_2_out;
  wire [7:0] and_5_out, and_6_out, and_7_out, and_8_out;
  wire [7:7] and_1_out, and_2_out, and_3_out, and_4_out;

  not not_1 (not_1_out, S1);
  not not_2 (not_2_out, S0);
  and and_1 (and_1_out[7], not_1_out, not_2_out);
  and and_2 (and_2_out[7], not_1_out, S0);
  and and_3 (and_3_out[7], S1, not_2_out);
  and and_4 (and_4_out[7], S1, S0);
  assign and_5_out = I0 & {8{and_1_out[7]}};  // AND_Gate and_5, 8 bits wide
  assign and_6_out = I1 & {8{and_2_out[7]}};  // AND_Gate and_6, 8 bits wide
  assign and_7_out = I2 & {8{and_3_out[7]}};  // AND_Gate and_7, 8 bits wide
  assign and_8_out = I3 & {8{and_4_out[7]}};  // AND_Gate and_8, 8 bits wide
  assign Y = and_5_out | and_6_out | and_7_out | and_8_out;  // OR_Gate or_1, 8 bits wide

  // Notes on the sheet:
  //   MUX4_8: Y = I[S1S0]  (S=00->I0, 01->I1, 10->I2, 11->I3)
  //   Decodificacao: e0=S1'S0'  e1=S1'S0  e2=S1S0'  e3=S1S0 ; cada e_k vira mascara de 8 bits no distribuidor
  //   LEGENDA: MUX4_8 = Multiplexador 4 entradas x 8 bits (Componente 02)
  //   I0..I3 = as 4 entradas de 8 bits
  //   S1 S0 = seletor: 00->I0, 01->I1, 10->I2, 11->I3
  //   Y = saida (a entrada escolhida)
endmodule

module MUX4_1 (
  input  I0,
  input  I1,
  input  I2,
  input  I3,
  input  S1,
  input  S0,
  output Y
);

  wire and_1_out, and_2_out, and_3_out, and_4_out, not_1_out, not_2_out;

  not not_1 (not_1_out, S1);
  not not_2 (not_2_out, S0);
  and and_1 (and_1_out, not_1_out, I0, not_2_out);
  and and_2 (and_2_out, not_1_out, I1, S0);
  and and_3 (and_3_out, S1, I2, not_2_out);
  and and_4 (and_4_out, S1, I3, S0);
  or or_1 (Y, and_1_out, and_2_out, and_3_out, and_4_out);

  // Notes on the sheet:
  //   MUX4_1: Y = I[S1 S0] (1 bit), feito com portas
  //   LEGENDA: MUX4_1 = Multiplexador 4 entradas x 1 bit
  //   I0..I3 = entradas
  //   S1 S0 = seletor
  //   Y = entrada escolhida
endmodule

module FF_D (
  input  set,
  input  clock,
  input  data,
  input  reset,
  output Q,
  output Qn
);

  wire nand_1_out, nand_2_out, nand_3_out, nand_4_out, not_1_out, not_2_out;

  not not_1 (not_1_out, set);
  not not_2 (not_2_out, reset);
  nand nand_1 (nand_1_out, not_1_out, nand_4_out, nand_2_out);
  nand nand_2 (nand_2_out, nand_1_out, clock, not_2_out);
  nand nand_3 (nand_3_out, nand_2_out, clock, nand_4_out);
  nand nand_4 (nand_4_out, nand_3_out, data, not_2_out);
  nand nand_5 (Q, not_1_out, nand_2_out, Qn);
  nand nand_6 (Qn, Q, nand_3_out, not_2_out);

  // Notes on the sheet:
  //   LEGENDA: FF_D = Flip-flop D (Componente 01): guarda 1 bit
  //   set = forca Q=1
  //   reset = forca Q=0 (zera)
  //   clock = relogio: grava 'data' na subida (0->1)
  //   data = bit a ser guardado
  //   Q = valor guardado
  //   Qn = Q invertido
endmodule

module DEC_7SEG_S (
  input  A,
  input  B,
  input  C,
  input  D,
  output seg_a,
  output seg_b,
  output seg_c,
  output seg_d,
  output seg_e,
  output seg_f,
  output seg_g
);

  wire and_1_out, and_2_out, and_3_out, and_4_out, and_5_out, and_6_out, and_7_out, and_8_out, and_9_out,
       not_1_out, not_2_out, not_3_out;

  not not_1 (not_1_out, B);
  not not_2 (not_2_out, C);
  not not_3 (not_3_out, D);
  and and_1 (and_1_out, B, D);
  and and_2 (and_2_out, not_1_out, not_3_out);
  and and_3 (and_3_out, not_2_out, not_3_out);
  and and_4 (and_4_out, C, D);
  and and_5 (and_5_out, not_1_out, C);
  and and_6 (and_6_out, C, not_3_out);
  and and_7 (and_7_out, B, not_2_out, D);
  and and_8 (and_8_out, B, not_2_out);
  and and_9 (and_9_out, B, not_3_out);
  or or_1 (seg_a, A, C, and_1_out, and_2_out);
  or or_2 (seg_b, not_1_out, and_3_out, and_4_out);
  or or_3 (seg_c, B, not_2_out, D);
  or or_4 (seg_d, A, and_2_out, and_5_out, and_6_out, and_7_out);
  or or_5 (seg_e, and_2_out, and_6_out);
  or or_6 (seg_f, A, and_3_out, and_8_out, and_9_out);
  or or_7 (seg_g, A, and_5_out, and_8_out, and_6_out);

  // Notes on the sheet:
  //   DEC_7SEG: entrada ABCD (A = MSB), saidas a..g ativas em 1 (0 a 9; 10-15 indiferentes)
  //   LEGENDA: DEC_7SEG = Decodificador de 7 segmentos (Componente 16)
  //   A B C D = numero de 4 bits (A = bit mais alto)
  //   seg_a..seg_g = segmentos acesos no display
endmodule

module SOMADOR8 (
  input  [7:0] A,
  input  [7:0] B,
  input  Cin,
  output [7:0] S,
  output Cout
);

  wire and_1_out, and_2_out, and_3_out, and_5_out, and_6_out, and_7_out, and_9_out, and_10_out, and_11_out,
       and_13_out, and_14_out, and_15_out, and_17_out, and_18_out, and_19_out, and_21_out, and_22_out,
       and_23_out, and_25_out, and_26_out, and_27_out, and_29_out, and_30_out, and_31_out, not_1_out,
       not_2_out, not_3_out, not_4_out, not_5_out, not_6_out, not_7_out, not_8_out, not_9_out, not_10_out,
       not_11_out, not_12_out, not_13_out, not_14_out, not_15_out, not_16_out, or_1_out, or_2_out, or_3_out,
       or_4_out, or_5_out, or_6_out, or_7_out, or_8_out, or_9_out, or_10_out, or_11_out, or_12_out,
       or_13_out, or_14_out, or_15_out, or_16_out, or_17_out, or_18_out, or_19_out, or_20_out, or_21_out,
       or_22_out, or_23_out;

  or or_1 (or_1_out, A[0], B[0]);
  and and_1 (and_1_out, A[0], B[0]);
  not not_1 (not_1_out, and_1_out);
  and and_2 (and_2_out, or_1_out, not_1_out);
  or or_2 (or_2_out, and_2_out, Cin);
  and and_3 (and_3_out, and_2_out, Cin);
  not not_2 (not_2_out, and_3_out);
  and and_4 (S[0], or_2_out, not_2_out);
  or or_3 (or_3_out, and_1_out, and_3_out);
  or or_4 (or_4_out, A[1], B[1]);
  and and_5 (and_5_out, A[1], B[1]);
  not not_3 (not_3_out, and_5_out);
  and and_6 (and_6_out, or_4_out, not_3_out);
  or or_5 (or_5_out, and_6_out, or_3_out);
  and and_7 (and_7_out, and_6_out, or_3_out);
  not not_4 (not_4_out, and_7_out);
  and and_8 (S[1], or_5_out, not_4_out);
  or or_6 (or_6_out, and_5_out, and_7_out);
  or or_7 (or_7_out, A[2], B[2]);
  and and_9 (and_9_out, A[2], B[2]);
  not not_5 (not_5_out, and_9_out);
  and and_10 (and_10_out, or_7_out, not_5_out);
  or or_8 (or_8_out, and_10_out, or_6_out);
  and and_11 (and_11_out, and_10_out, or_6_out);
  not not_6 (not_6_out, and_11_out);
  and and_12 (S[2], or_8_out, not_6_out);
  or or_9 (or_9_out, and_9_out, and_11_out);
  or or_10 (or_10_out, A[3], B[3]);
  and and_13 (and_13_out, A[3], B[3]);
  not not_7 (not_7_out, and_13_out);
  and and_14 (and_14_out, or_10_out, not_7_out);
  or or_11 (or_11_out, and_14_out, or_9_out);
  and and_15 (and_15_out, and_14_out, or_9_out);
  not not_8 (not_8_out, and_15_out);
  and and_16 (S[3], or_11_out, not_8_out);
  or or_12 (or_12_out, and_13_out, and_15_out);
  or or_13 (or_13_out, A[4], B[4]);
  and and_17 (and_17_out, A[4], B[4]);
  not not_9 (not_9_out, and_17_out);
  and and_18 (and_18_out, or_13_out, not_9_out);
  or or_14 (or_14_out, and_18_out, or_12_out);
  and and_19 (and_19_out, and_18_out, or_12_out);
  not not_10 (not_10_out, and_19_out);
  and and_20 (S[4], or_14_out, not_10_out);
  or or_15 (or_15_out, and_17_out, and_19_out);
  or or_16 (or_16_out, A[5], B[5]);
  and and_21 (and_21_out, A[5], B[5]);
  not not_11 (not_11_out, and_21_out);
  and and_22 (and_22_out, or_16_out, not_11_out);
  or or_17 (or_17_out, and_22_out, or_15_out);
  and and_23 (and_23_out, and_22_out, or_15_out);
  not not_12 (not_12_out, and_23_out);
  and and_24 (S[5], or_17_out, not_12_out);
  or or_18 (or_18_out, and_21_out, and_23_out);
  or or_19 (or_19_out, A[6], B[6]);
  and and_25 (and_25_out, A[6], B[6]);
  not not_13 (not_13_out, and_25_out);
  and and_26 (and_26_out, or_19_out, not_13_out);
  or or_20 (or_20_out, and_26_out, or_18_out);
  and and_27 (and_27_out, and_26_out, or_18_out);
  not not_14 (not_14_out, and_27_out);
  and and_28 (S[6], or_20_out, not_14_out);
  or or_21 (or_21_out, and_25_out, and_27_out);
  or or_22 (or_22_out, A[7], B[7]);
  and and_29 (and_29_out, A[7], B[7]);
  not not_15 (not_15_out, and_29_out);
  and and_30 (and_30_out, or_22_out, not_15_out);
  or or_23 (or_23_out, and_30_out, or_21_out);
  and and_31 (and_31_out, and_30_out, or_21_out);
  not not_16 (not_16_out, and_31_out);
  and and_32 (S[7], or_23_out, not_16_out);
  or or_24 (Cout, and_29_out, and_31_out);

  // Notes on the sheet:
  //   SOMADOR8: S = A + B + Cin (8 somadores completos em cascata, XOR feito com AND/OR/NOT)
  //   LEGENDA: SOMADOR8 = Somador de 8 bits (Componente 08)
  //   A, B = numeros de 8 bits
  //   Cin = vai-um de entrada
  //   S = A + B + Cin
  //   Cout = vai-um de saida
endmodule

module SEL_ENDERECO (
  input  [5:0] ADDR,
  input  MODO,
  input  V2,
  input  V1,
  input  V0,
  output T2,
  output T1,
  output T0,
  output I1,
  output I0,
  output OF
);

  wire and_1_out, and_2_out, and_3_out, and_4_out, and_5_out, and_6_out, not_1_out;

  not not_1 (not_1_out, MODO);
  // NOT_Gate not_2 has open pins: in=ADDR[5], out=open
  // NOT_Gate not_3 has open pins: in=ADDR[4], out=open
  // NOT_Gate not_4 has open pins: in=ADDR[3], out=open
  // NOT_Gate not_5 has open pins: in=ADDR[2], out=open
  // NOT_Gate not_6 has open pins: in=ADDR[1], out=open
  // NOT_Gate not_7 has open pins: in=ADDR[0], out=open
  // NOT_Gate not_8 has open pins: in=V2, out=open
  // NOT_Gate not_9 has open pins: in=V1, out=open
  // NOT_Gate not_10 has open pins: in=V0, out=open
  and and_1 (and_1_out, not_1_out, ADDR[5]);
  and and_2 (and_2_out, MODO, V2);
  and and_3 (and_3_out, not_1_out, ADDR[4]);
  and and_4 (and_4_out, MODO, V1);
  and and_5 (and_5_out, not_1_out, ADDR[3]);
  and and_6 (and_6_out, MODO, V0);
  and and_7 (I1, not_1_out, ADDR[2]);
  and and_8 (I0, not_1_out, ADDR[1]);
  and and_9 (OF, not_1_out, ADDR[0]);
  or or_1 (T2, and_1_out, and_2_out);
  or or_2 (T1, and_3_out, and_4_out);
  or or_3 (T0, and_5_out, and_6_out);

  // Notes on the sheet:
  //   LEGENDA: SEL_ENDERECO = Selecao e divisao do endereco
  //   ADDR = endereco
  //   MODO = 0 normal, 1 primos
  //   V2..V0 = contador v
  //   T2 T1 T0 = ROTULO
  //   I1 I0 = INDICE (linha)
  //   OF = DESLOCAMENTO (byte)
  //   SEL_ENDERECO com FIOS DIRETOS (sem tuneis). Cruzamento sem ponto = nao ligado.
endmodule

module COMPARADOR_ROTULO (
  input  T2,
  input  T1,
  input  T0,
  input  SS2,
  input  SS1,
  input  SS0,
  input  VSEL,
  output ACERTO,
  output IGUAIS
);

  wire or_1_out, xor2_1_s, xor2_2_s, xor2_3_s;

  or or_1 (or_1_out, xor2_1_s, xor2_2_s, xor2_3_s);
  not not_1 (IGUAIS, or_1_out);
  and and_1 (ACERTO, IGUAIS, VSEL);
  xor2 xor2_1 (.x(T0), .Y(SS0), .S(xor2_1_s));
  xor2 xor2_2 (.x(T1), .Y(SS1), .S(xor2_2_s));
  xor2 xor2_3 (.x(T2), .Y(SS2), .S(xor2_3_s));

  // Notes on the sheet:
  //   LEGENDA: COMPARADOR_ROTULO = Compara o rotulo do
  //   endereco com o guardado
  //   T2..T0 = rotulo do endereco
  //   SS2..SS0 = rotulo guardado na linha
  //   VSEL = bit de validade da linha
  //   IGUAIS = 1 se os rotulos sao iguais
  //   ACERTO = IGUAIS . VSEL
  //   COMPARADOR_ROTULO com FIOS DIRETOS (sem tuneis). Cruzamento sem ponto = nao ligado.
endmodule

module CONTROLE_ACESSO (
  input  ACERTO,
  input  MODO,
  input  PRIMO,
  input  I1,
  input  I0,
  output HIT,
  output WE0,
  output WE1,
  output WE2,
  output WE3
);

  wire and_4_out, and_5_out, and_7_out, and_9_out, and_10_out, not_1_out, not_2_out, not_3_out, not_4_out,
       or_1_out;

  not not_1 (not_1_out, ACERTO);
  and and_1 (WE0, and_5_out, and_4_out);
  not not_2 (not_2_out, I1);
  not not_3 (not_3_out, MODO);
  not not_4 (not_4_out, I0);
  and and_2 (WE1, and_5_out, and_7_out);
  or or_1 (or_1_out, not_3_out, PRIMO);
  and and_3 (WE2, and_5_out, and_9_out);
  and and_4 (and_4_out, not_2_out, not_4_out);
  and and_5 (and_5_out, not_1_out, or_1_out);
  and and_6 (WE3, and_5_out, and_10_out);
  and and_7 (and_7_out, not_2_out, I0);
  and and_8 (HIT, ACERTO, or_1_out);
  and and_9 (and_9_out, I1, not_4_out);
  and and_10 (and_10_out, I1, I0);

  // Notes on the sheet:
  //   LEGENDA: CONTROLE_ACESSO = Decide o que o pulso de relogio faz
  //   EN = MODO' + PRIMO (o acesso conta)
  //   MISS = falta (NOT ACERTO)
  //   HIT = ACERTO . EN -> soma 1 no contador
  //   WE0..WE3 = grava a linha 0..3 numa falta (WR = falta . EN)
  //   CONTROLE_ACESSO com FIOS DIRETOS (sem tuneis). Cruzamento sem ponto = nao ligado.
endmodule

module VALIDADE (
  input  WE0,
  input  WE1,
  input  WE2,
  input  WE3,
  input  CLK,
  input  CLR,
  input  I1,
  input  I0,
  output VSEL,
  output VL0,
  output VL1,
  output VL2,
  output VL3
);

  wire or_1_out, or_2_out, or_3_out, or_4_out;

  or or_1 (or_1_out, VL0, WE0);
  or or_2 (or_2_out, VL1, WE1);
  or or_3 (or_3_out, VL2, WE2);
  or or_4 (or_4_out, VL3, WE3);
  FF_D ff_d_1 (.set(1'b0), .clock(CLK), .data(or_1_out), .reset(CLR), .Q(VL0));  // open: Qn
  MUX4_1 mux4_1_1 (.I0(VL0), .I1(VL1), .I2(VL2), .I3(VL3), .S1(I1), .S0(I0), .Y(VSEL));
  FF_D ff_d_2 (.set(1'b0), .clock(CLK), .data(or_2_out), .reset(CLR), .Q(VL1));  // open: Qn
  FF_D ff_d_3 (.set(1'b0), .clock(CLK), .data(or_3_out), .reset(CLR), .Q(VL2));  // open: Qn
  FF_D ff_d_4 (.set(1'b0), .clock(CLK), .data(or_4_out), .reset(CLR), .Q(VL3));  // open: Qn

  // Notes on the sheet:
  //   LEGENDA: VALIDADE = Bits de validade das 4
  //   linhas (4 flip-flops D)
  //   WE0..WE3 = carregar a linha k
  //   CLR = zera todos (cache vazia)
  //   I1 I0 = indice
  //   VSEL = validade da linha atual
  //   VL0..VL3 = validade de cada linha
  //   VALIDADE com FIOS DIRETOS (sem tuneis). Cruzamento sem ponto = nao ligado.
endmodule

module ROTULOS (
  input  T2,
  input  T1,
  input  T0,
  input  WE0,
  input  WE1,
  input  WE2,
  input  WE3,
  input  CLK,
  input  CLR,
  input  I1,
  input  I0,
  output SS2,
  output SS1,
  output SS0,
  output [2:0] TAG0,
  output [2:0] TAG1,
  output [2:0] TAG2,
  output [2:0] TAG3
);

  Register #(.width(3)) REG_ROT0 (.D({T2, T1, T0}), .en(WE0), .clk(CLK), .Q(TAG0), .clr(CLR));
  Register #(.width(3)) REG_ROT1 (.D({T2, T1, T0}), .en(WE1), .clk(CLK), .Q(TAG1), .clr(CLR));
  Register #(.width(3)) REG_ROT2 (.D({T2, T1, T0}), .en(WE2), .clk(CLK), .Q(TAG2), .clr(CLR));
  Register #(.width(3)) REG_ROT3 (.D({T2, T1, T0}), .en(WE3), .clk(CLK), .Q(TAG3), .clr(CLR));
  MUX4_1 mux4_1_1 (.I0(TAG0[0]), .I1(TAG1[0]), .I2(TAG2[0]), .I3(TAG3[0]), .S1(I1), .S0(I0), .Y(SS0));
  MUX4_1 mux4_1_2 (.I0(TAG0[1]), .I1(TAG1[1]), .I2(TAG2[1]), .I3(TAG3[1]), .S1(I1), .S0(I0), .Y(SS1));
  MUX4_1 mux4_1_3 (.I0(TAG0[2]), .I1(TAG1[2]), .I2(TAG2[2]), .I3(TAG3[2]), .S1(I1), .S0(I0), .Y(SS2));

  // Notes on the sheet:
  //   LEGENDA: ROTULOS = Rotulos guardados (4 registradores de 3 bits)
  //   T2..T0 = rotulo novo
  //   WE0..WE3 = gravar na linha k
  //   I1 I0 = indice
  //   SS2..SS0 = rotulo da linha atual
  //   TAG0..TAG3 = rotulo de cada linha
  //   ROTULOS com FIOS DIRETOS (sem tuneis). Cruzamento sem ponto = nao ligado.
endmodule

module DADOS_CACHE (
  input  T2,
  input  T1,
  input  T0,
  input  I1,
  input  I0,
  input  OF,
  input  WE0,
  input  WE1,
  input  WE2,
  input  WE3,
  input  CLK,
  input  CLR,
  output [7:0] DADO
);

  wire [7:0] MEM_PRINCIPAL_data, MEM_PRINCIPAL_data_2, mux4_8_1_y, mux4_8_2_y, REG_HI0_q, REG_HI1_q,
       REG_HI2_q, REG_HI3_q, REG_LO0_q, REG_LO1_q, REG_LO2_q, REG_LO3_q;

  ROM #(.addrWidth(5), .dataWidth(16)) MEM_PRINCIPAL (
    .addr({T2, T1, T0, I1, I0}), .data({MEM_PRINCIPAL_data_2, MEM_PRINCIPAL_data}));
  Register REG_LO0 (.D(MEM_PRINCIPAL_data), .en(WE0), .clk(CLK), .Q(REG_LO0_q), .clr(CLR));
  Register REG_HI0 (.D(MEM_PRINCIPAL_data_2), .en(WE0), .clk(CLK), .Q(REG_HI0_q), .clr(CLR));
  Register REG_LO1 (.D(MEM_PRINCIPAL_data), .en(WE1), .clk(CLK), .Q(REG_LO1_q), .clr(CLR));
  Register REG_HI1 (.D(MEM_PRINCIPAL_data_2), .en(WE1), .clk(CLK), .Q(REG_HI1_q), .clr(CLR));
  Register REG_LO2 (.D(MEM_PRINCIPAL_data), .en(WE2), .clk(CLK), .Q(REG_LO2_q), .clr(CLR));
  Register REG_HI2 (.D(MEM_PRINCIPAL_data_2), .en(WE2), .clk(CLK), .Q(REG_HI2_q), .clr(CLR));
  Register REG_LO3 (.D(MEM_PRINCIPAL_data), .en(WE3), .clk(CLK), .Q(REG_LO3_q), .clr(CLR));
  Register REG_HI3 (.D(MEM_PRINCIPAL_data_2), .en(WE3), .clk(CLK), .Q(REG_HI3_q), .clr(CLR));
  MUX4_8 mux4_8_1 (.I0(REG_LO0_q), .I1(REG_LO1_q), .I2(REG_LO2_q), .I3(REG_LO3_q), .S1(I1), .S0(I0), .Y(mux4_8_1_y));
  MUX4_8 mux4_8_2 (.I0(REG_HI0_q), .I1(REG_HI1_q), .I2(REG_HI2_q), .I3(REG_HI3_q), .S1(I1), .S0(I0), .Y(mux4_8_2_y));
  MUX4_8 mux4_8_3 (.I0(mux4_8_1_y), .I1(mux4_8_2_y), .I2({8{1'b0}}), .I3({8{1'b0}}), .S1(1'b0), .S0(OF), .Y(DADO));

  // Notes on the sheet:
  //   LEGENDA: DADOS_CACHE = Memoria principal + 4 linhas de 2 bytes
  //   T2..T0, I1 I0 = bloco
  //   OF = qual byte do bloco
  //   WE0..WE3 = carregar linha
  //   MEM_PRINCIPAL = ROM com 32 blocos de 2 bytes
  //   DADO = byte lido da cache
  //   contents of MEM_PRINCIPAL (hex, n*v repeats v):
  //   100 302 504 706 908 b0a d0c f0e 1110 1312 1514 1716 1918 1b1a 1d1c 1f1e 2120 2322 2524 2726 2928
  //   2b2a 2d2c 2f2e 3130 3332 3534 3736 3938 3b3a 3d3c 3f3e
  //   DADOS_CACHE com FIOS DIRETOS (sem tuneis). Cruzamento sem ponto = nao ligado.
endmodule

module CONTADOR_4 (
  input  HIT,
  input  CLK,
  input  CLR,
  output C3,
  output C2,
  output C1,
  output C0
);

  wire and_1_out, and_2_out, and_3_out, and_4_out, and_5_out, and_6_out, and_7_out, and_8_out, and_9_out,
       and_10_out, and_11_out, and_12_out, and_13_out, and_14_out, not_1_out, not_2_out, not_3_out,
       not_4_out, not_5_out, or_1_out, or_2_out, or_3_out, or_4_out;

  not not_1 (not_1_out, C3);
  not not_2 (not_2_out, C2);
  not not_3 (not_3_out, C1);
  not not_4 (not_4_out, C0);
  not not_5 (not_5_out, HIT);
  and and_1 (and_1_out, C0, not_5_out);
  and and_2 (and_2_out, not_4_out, HIT);
  and and_3 (and_3_out, C1, not_5_out);
  and and_4 (and_4_out, C1, not_4_out);
  and and_5 (and_5_out, not_3_out, C0, HIT);
  and and_6 (and_6_out, C2, not_5_out);
  and and_7 (and_7_out, C2, not_4_out);
  and and_8 (and_8_out, C2, not_3_out);
  and and_9 (and_9_out, not_2_out, C1, C0, HIT);
  and and_10 (and_10_out, C3, not_5_out);
  and and_11 (and_11_out, C3, not_4_out);
  and and_12 (and_12_out, C3, not_3_out);
  and and_13 (and_13_out, C3, not_2_out);
  and and_14 (and_14_out, not_1_out, C2, C1, C0, HIT);
  or or_1 (or_1_out, and_1_out, and_2_out);
  or or_2 (or_2_out, and_3_out, and_4_out, and_5_out);
  or or_3 (or_3_out, and_6_out, and_7_out, and_8_out, and_9_out);
  or or_4 (or_4_out, and_10_out, and_11_out, and_12_out, and_13_out, and_14_out);
  FF_D ff_d_1 (.set(1'b0), .clock(CLK), .data(or_1_out), .reset(CLR), .Q(C0));  // open: Qn
  FF_D ff_d_2 (.set(1'b0), .clock(CLK), .data(or_2_out), .reset(CLR), .Q(C1));  // open: Qn
  FF_D ff_d_3 (.set(1'b0), .clock(CLK), .data(or_3_out), .reset(CLR), .Q(C2));  // open: Qn
  FF_D ff_d_4 (.set(1'b0), .clock(CLK), .data(or_4_out), .reset(CLR), .Q(C3));  // open: Qn

  // Notes on the sheet:
  //   LEGENDA: CONTADOR_4 = Contador de acertos de 4 bits (Componente 13)
  //   HIT = 1 soma 1 no pulso
  //   CLR = zera
  //   C3..C0 = contagem
  //   CONTADOR_4 com FIOS DIRETOS (sem tuneis). Cruzamento sem ponto = nao ligado.
endmodule

module CONTADOR_3 (
  input  EN,
  input  CLK,
  input  CLR,
  output V2,
  output V1,
  output V0
);

  wire and_1_out, and_2_out, and_3_out, and_4_out, and_5_out, and_6_out, and_7_out, and_8_out, and_9_out,
       not_1_out, not_2_out, not_3_out, not_4_out, or_1_out, or_2_out, or_3_out;

  not not_1 (not_1_out, V2);
  not not_2 (not_2_out, V1);
  not not_3 (not_3_out, V0);
  not not_4 (not_4_out, EN);
  and and_1 (and_1_out, V0, not_4_out);
  and and_2 (and_2_out, not_3_out, EN);
  and and_3 (and_3_out, V1, not_4_out);
  and and_4 (and_4_out, V1, not_3_out);
  and and_5 (and_5_out, not_2_out, V0, EN);
  and and_6 (and_6_out, V2, not_4_out);
  and and_7 (and_7_out, V2, not_3_out);
  and and_8 (and_8_out, V2, not_2_out);
  and and_9 (and_9_out, not_1_out, V1, V0, EN);
  or or_1 (or_1_out, and_1_out, and_2_out);
  or or_2 (or_2_out, and_3_out, and_4_out, and_5_out);
  or or_3 (or_3_out, and_6_out, and_7_out, and_8_out, and_9_out);
  FF_D ff_d_1 (.set(1'b0), .clock(CLK), .data(or_1_out), .reset(CLR), .Q(V0));  // open: Qn
  FF_D ff_d_2 (.set(1'b0), .clock(CLK), .data(or_2_out), .reset(CLR), .Q(V1));  // open: Qn
  FF_D ff_d_3 (.set(1'b0), .clock(CLK), .data(or_3_out), .reset(CLR), .Q(V2));  // open: Qn

  // Notes on the sheet:
  //   LEGENDA: CONTADOR_3 = Contador v de 3 bits
  //   (Componente 13)
  //   EN = 1 avanca no pulso
  //   CLR = zera
  //   V2..V0 = valor v (0 a 7)
  //   CONTADOR_3 com FIOS DIRETOS (sem tuneis). Cruzamento sem ponto = nao ligado.
endmodule

module CACHE_PARTE1 (
  input  [5:0] ADDR,
  input  CLK,
  input  CLR,
  input  MODO,
  input  [7:0] DESLOC,
  output ACERTO,
  output [7:0] DADO,
  output ACERTOS_C3,
  output ACERTOS_C2,
  output ACERTOS_C1,
  output ACERTOS_C0,
  output VAL0,
  output VAL1,
  output VAL2,
  output VAL3,
  output [2:0] ROT0,
  output [2:0] ROT1,
  output [2:0] ROT2,
  output [2:0] ROT3,
  output V2,
  output V1,
  output V0,
  output PRIMO
);

  wire controle_acesso_1_hit, controle_acesso_1_we0, controle_acesso_1_we1, controle_acesso_1_we2,
       controle_acesso_1_we3, dec_7seg_s_1_seg_a, dec_7seg_s_1_seg_b, dec_7seg_s_1_seg_c, dec_7seg_s_1_seg_d,
       dec_7seg_s_1_seg_e, dec_7seg_s_1_seg_f, dec_7seg_s_1_seg_g, rotulos_1_ss0, rotulos_1_ss1,
       rotulos_1_ss2, sel_endereco_1_i0, sel_endereco_1_i1, sel_endereco_1_of, sel_endereco_1_t0,
       sel_endereco_1_t1, sel_endereco_1_t2, validade_1_vsel;
  wire [7:0] somador8_1_s;

  LED LED_ACERTO (.in(ACERTO));
  _7_Segment_Display u_7_segment_display_1 (
    .g(dec_7seg_s_1_seg_g), .f(dec_7seg_s_1_seg_f), .a(dec_7seg_s_1_seg_a), .b(dec_7seg_s_1_seg_b),
    .e(dec_7seg_s_1_seg_e), .d(dec_7seg_s_1_seg_d), .c(dec_7seg_s_1_seg_c));  // open: dp
  CONTADOR_3 contador_3_1 (.EN(MODO), .CLK(CLK), .CLR(CLR), .V2(V2), .V1(V1), .V0(V0));
  SEL_ENDERECO sel_endereco_1 (
    .ADDR(somador8_1_s[5:0]), .MODO(MODO), .V2(V2), .V1(V1), .V0(V0), .T2(sel_endereco_1_t2),
    .T1(sel_endereco_1_t1), .T0(sel_endereco_1_t0), .I1(sel_endereco_1_i1), .I0(sel_endereco_1_i0),
    .OF(sel_endereco_1_of));
  ROTULOS rotulos_1 (
    .T2(sel_endereco_1_t2), .T1(sel_endereco_1_t1), .T0(sel_endereco_1_t0), .WE0(controle_acesso_1_we0),
    .WE1(controle_acesso_1_we1), .WE2(controle_acesso_1_we2), .WE3(controle_acesso_1_we3), .CLK(CLK),
    .CLR(CLR), .I1(sel_endereco_1_i1), .I0(sel_endereco_1_i0), .SS2(rotulos_1_ss2), .SS1(rotulos_1_ss1),
    .SS0(rotulos_1_ss0), .TAG0(ROT0), .TAG1(ROT1), .TAG2(ROT2), .TAG3(ROT3));
  COMPARADOR_ROTULO comparador_rotulo_1 (
    .T2(sel_endereco_1_t2), .T1(sel_endereco_1_t1), .T0(sel_endereco_1_t0), .SS2(rotulos_1_ss2),
    .SS1(rotulos_1_ss1), .SS0(rotulos_1_ss0), .VSEL(validade_1_vsel), .ACERTO(ACERTO));  // open: IGUAIS
  Primo4 primo4_1 (.A(1'b0), .B(V2), .C(V1), .D(V0), .P(PRIMO));
  CONTROLE_ACESSO controle_acesso_1 (
    .ACERTO(ACERTO), .MODO(MODO), .PRIMO(PRIMO), .I1(sel_endereco_1_i1), .I0(sel_endereco_1_i0),
    .HIT(controle_acesso_1_hit), .WE0(controle_acesso_1_we0), .WE1(controle_acesso_1_we1),
    .WE2(controle_acesso_1_we2), .WE3(controle_acesso_1_we3));
  VALIDADE validade_1 (
    .WE0(controle_acesso_1_we0), .WE1(controle_acesso_1_we1), .WE2(controle_acesso_1_we2),
    .WE3(controle_acesso_1_we3), .CLK(CLK), .CLR(CLR), .I1(sel_endereco_1_i1), .I0(sel_endereco_1_i0),
    .VSEL(validade_1_vsel), .VL0(VAL0), .VL1(VAL1), .VL2(VAL2), .VL3(VAL3));
  SOMADOR8 somador8_1 (.A({2'b00, ADDR}), .B(DESLOC), .Cin(1'b0), .S(somador8_1_s));  // open: Cout
  DADOS_CACHE dados_cache_1 (
    .T2(sel_endereco_1_t2), .T1(sel_endereco_1_t1), .T0(sel_endereco_1_t0), .I1(sel_endereco_1_i1),
    .I0(sel_endereco_1_i0), .OF(sel_endereco_1_of), .WE0(controle_acesso_1_we0), .WE1(controle_acesso_1_we1),
    .WE2(controle_acesso_1_we2), .WE3(controle_acesso_1_we3), .CLK(CLK), .CLR(CLR), .DADO(DADO));
  CONTADOR_4 contador_4_1 (
    .HIT(controle_acesso_1_hit), .CLK(CLK), .CLR(CLR), .C3(ACERTOS_C3), .C2(ACERTOS_C2), .C1(ACERTOS_C1),
    .C0(ACERTOS_C0));
  DEC_7SEG_S dec_7seg_s_1 (
    .A(ACERTOS_C3), .B(ACERTOS_C2), .C(ACERTOS_C1), .D(ACERTOS_C0), .seg_a(dec_7seg_s_1_seg_a),
    .seg_b(dec_7seg_s_1_seg_b), .seg_c(dec_7seg_s_1_seg_c), .seg_d(dec_7seg_s_1_seg_d),
    .seg_e(dec_7seg_s_1_seg_e), .seg_f(dec_7seg_s_1_seg_f), .seg_g(dec_7seg_s_1_seg_g));

  // Notes on the sheet:
  //   LEGENDA: CACHE_PARTE1 = Cache de mapeamento direto, 4 linhas x 2 bytes
  //   ADDR = endereco de 6 bits: ROTULO A5A4A3, INDICE A2A1, DESLOCAMENTO A0
  //   DESLOC = valor somado ao endereco (endereco efetivo = ADDR + DESLOC)
  //   CLK = relogio: o pulso conclui o acesso
  //   CLR = zera a cache (invalida tudo)
  //   MODO = 0 usa ADDR, 1 teste dos primos (endereco = v << 3)
  //   ACERTO = 1 se o dado ja estava na cache (olhar ANTES do pulso)
  //   DADO = byte lido
  //   ACERTOS_C3..C0 = contador de acertos (display)
  //   VAL0..VAL3 = bit de validade de cada linha
  //   ROT0..ROT3 = rotulo guardado
  //   V2 V1 V0 = valor v do contador
  //   PRIMO = 1 se v e primo
  //   CACHE_PARTE1 com FIOS DIRETOS (sem tuneis). Cruzamento sem ponto = nao ligado.
endmodule
