// Logisim project parte1_memoria.circ as structural Verilog
module xor2 (
  input  x,
  input  Y,
  output S
);

  wire and_1_out, and_2_out, not_1_out, not_2_out;

  not not_1 (not_1_out, x);
  not not_2 (not_2_out, Y);
  and and_1 (and_1_out, x, not_2_out);
  and and_2 (and_2_out, not_1_out, Y);
  or or_1 (S, and_1_out, and_2_out);

  // Notes on the sheet:
  //   LEGENDA: xor2 = XOR feito com AND, OR e NOT (Componente 03)
  //   S = x.Y' + x'.Y  ->  S=1 quando as entradas sao DIFERENTES
endmodule

module PARIDADE_IMPAR (
  input  [7:0] D,
  output P
);

  wire xor2_1_s, xor2_2_s, xor2_3_s, xor2_4_s, xor2_5_s, xor2_6_s, xor2_7_s;

  xor2 xor2_1 (.x(D[0]), .Y(D[1]), .S(xor2_1_s));
  xor2 xor2_2 (.x(D[2]), .Y(D[3]), .S(xor2_2_s));
  xor2 xor2_3 (.x(D[4]), .Y(D[5]), .S(xor2_3_s));
  xor2 xor2_4 (.x(D[6]), .Y(D[7]), .S(xor2_4_s));
  xor2 xor2_5 (.x(xor2_1_s), .Y(xor2_2_s), .S(xor2_5_s));
  xor2 xor2_6 (.x(xor2_3_s), .Y(xor2_4_s), .S(xor2_6_s));
  xor2 xor2_7 (.x(xor2_5_s), .Y(xor2_6_s), .S(xor2_7_s));
  not not_1 (P, xor2_7_s);

  // Notes on the sheet:
  //   LEGENDA: PARIDADE_IMPAR = Gerador de paridade impar (Componente 14)
  //   D = dado de 8 bits
  //   P = bit de paridade: faz o total de 1s (dado + P) ficar IMPAR
  //   Ex.: 0x55 tem quatro 1s -> P = 1
endmodule

module MUX4_8 (
  input  [7:0] I0,
  input  [7:0] I1,
  input  [7:0] I2,
  input  [7:0] I3,
  input  S1,
  input  S0,
  output [7:0] Y
);

  wire not_1_out, not_2_out;
  wire [7:0] and_5_out, and_6_out, and_7_out, and_8_out;
  wire [7:7] and_1_out, and_2_out, and_3_out, and_4_out;

  not not_1 (not_1_out, S1);
  not not_2 (not_2_out, S0);
  and and_1 (and_1_out[7], not_1_out, not_2_out);
  and and_2 (and_2_out[7], not_1_out, S0);
  and and_3 (and_3_out[7], S1, not_2_out);
  and and_4 (and_4_out[7], S1, S0);
  assign and_5_out = I0 & {8{and_1_out[7]}};  // AND_Gate and_5, 8 bits wide
  assign and_6_out = I1 & {8{and_2_out[7]}};  // AND_Gate and_6, 8 bits wide
  assign and_7_out = I2 & {8{and_3_out[7]}};  // AND_Gate and_7, 8 bits wide
  assign and_8_out = I3 & {8{and_4_out[7]}};  // AND_Gate and_8, 8 bits wide
  assign Y = and_5_out | and_6_out | and_7_out | and_8_out;  // OR_Gate or_1, 8 bits wide

  // Notes on the sheet:
  //   MUX4_8: Y = I[S1S0]  (S=00->I0, 01->I1, 10->I2, 11->I3)
  //   Decodificacao: e0=S1'S0'  e1=S1'S0  e2=S1S0'  e3=S1S0 ; cada e_k vira mascara de 8 bits no distribuidor
  //   LEGENDA: MUX4_8 = Multiplexador 4 entradas x 8 bits (Componente 02)
  //   I0..I3 = as 4 entradas de 8 bits
  //   S1 S0 = seletor: 00->I0, 01->I1, 10->I2, 11->I3
  //   Y = saida (a entrada escolhida)
endmodule

module Primo4 (
  input  A,
  input  B,
  input  C,
  input  D,
  output P
);

  wire and_1_out, and_2_out, and_3_out, and_4_out, not_1_out, not_2_out, not_3_out;

  not not_1 (not_1_out, A);
  not not_2 (not_2_out, B);
  not not_3 (not_3_out, C);
  and and_1 (and_1_out, not_1_out, not_2_out, C);
  and and_2 (and_2_out, not_1_out, B, D);
  and and_3 (and_3_out, not_2_out, C, D);
  and and_4 (and_4_out, B, not_3_out, D);
  or or_1 (P, and_1_out, and_2_out, and_3_out, and_4_out);

  // Notes on the sheet:
  //   LEGENDA: Primo4 = Detector de numero primo de 4 bits (Componente 17)
  //   A B C D = numero de 4 bits (A = bit mais alto)
  //   P = 1 se o numero e primo (2, 3, 5, 7, 11, 13)
endmodule

module DEC_7SEG (
  input  A,
  input  B,
  input  C,
  input  D
);

  wire and_1_out, and_2_out, and_3_out, and_4_out, and_5_out, and_6_out, and_7_out, and_8_out, and_9_out,
       not_1_out, not_2_out, not_3_out, or_1_out, or_2_out, or_3_out, or_4_out, or_5_out, or_6_out, or_7_out;

  not not_1 (not_1_out, B);
  not not_2 (not_2_out, C);
  not not_3 (not_3_out, D);
  and and_1 (and_1_out, B, D);
  and and_2 (and_2_out, not_1_out, not_3_out);
  and and_3 (and_3_out, not_2_out, not_3_out);
  and and_4 (and_4_out, C, D);
  and and_5 (and_5_out, not_1_out, C);
  and and_6 (and_6_out, C, not_3_out);
  and and_7 (and_7_out, B, not_2_out, D);
  and and_8 (and_8_out, B, not_2_out);
  and and_9 (and_9_out, B, not_3_out);
  or or_1 (or_1_out, A, C, and_1_out, and_2_out);
  or or_2 (or_2_out, not_1_out, and_3_out, and_4_out);
  or or_3 (or_3_out, B, not_2_out, D);
  or or_4 (or_4_out, A, and_2_out, and_5_out, and_6_out, and_7_out);
  or or_5 (or_5_out, and_2_out, and_6_out);
  or or_6 (or_6_out, A, and_3_out, and_8_out, and_9_out);
  or or_7 (or_7_out, A, and_5_out, and_8_out, and_6_out);
  _7_Segment_Display u_7_segment_display_1 (
    .g(or_7_out), .f(or_6_out), .a(or_1_out), .b(or_2_out), .e(or_5_out), .d(or_4_out), .c(or_3_out));  // open: dp

  // Notes on the sheet:
  //   DEC_7SEG: entrada ABCD (A = MSB), saidas a..g ativas em 1 (0 a 9; 10-15 indiferentes)
  //   LEGENDA: DEC_7SEG = Decodificador de 7 segmentos (Componente 16)
  //   A B C D = numero de 4 bits (A = bit mais alto)
  //   seg_a..seg_g = segmentos acesos no display
endmodule

module FF_D (
  input  set,
  input  clock,
  input  data,
  input  reset,
  output out_5,
  output out_6
);

  wire nand_1_out, nand_2_out, nand_3_out, nand_4_out, not_1_out, not_2_out;

  not not_1 (not_1_out, set);
  not not_2 (not_2_out, reset);
  nand nand_1 (nand_1_out, not_1_out, nand_4_out, nand_2_out);
  nand nand_2 (nand_2_out, nand_1_out, clock, not_2_out);
  nand nand_3 (nand_3_out, nand_2_out, clock, nand_4_out);
  nand nand_4 (nand_4_out, nand_3_out, data, not_2_out);
  nand nand_5 (out_5, not_1_out, nand_2_out, out_6);
  nand nand_6 (out_6, out_5, nand_3_out, not_2_out);

  // Notes on the sheet:
  //   LEGENDA: FF_D = Flip-flop D (Componente 01): guarda 1 bit
  //   set = forca Q=1
  //   reset = forca Q=0 (zera)
  //   clock = relogio: grava 'data' na subida (0->1)
  //   data = bit a ser guardado
  //   Q = valor guardado
  //   Qn = Q invertido
endmodule

module FF_JK (
  input  PRE,
  input  J,
  input  K,
  input  CLR,
  output Q,
  output Qn
);

  wire clock_1_out, nand_1_out, nand_2_out, nand_3_out, nand_4_out, nand_5_out, nand_7_out, not_1_out,
       not_2_out, not_3_out;

  Clock clock_1 (.out(clock_1_out));
  nand nand_1 (nand_1_out, Qn, J, clock_1_out);
  not not_1 (not_1_out, PRE);
  not not_2 (not_2_out, clock_1_out);
  nand nand_2 (nand_2_out, clock_1_out, K, Q);
  not not_3 (not_3_out, CLR);
  nand nand_3 (nand_3_out, not_1_out, nand_1_out, nand_4_out);
  nand nand_4 (nand_4_out, nand_3_out, nand_2_out, not_3_out);
  nand nand_5 (nand_5_out, nand_3_out, not_2_out);
  nand nand_6 (Q, nand_5_out, Qn);
  nand nand_7 (nand_7_out, not_2_out, nand_4_out);
  nand nand_8 (Qn, Q, nand_7_out);

  // Notes on the sheet:
  //   Flip-Flop-JK
  //   Este é um flip-flop jk, feito com preset e clear, aonde não podemos ligar ambos ao mesmo tempo.
  //   LEGENDA: FF_JK = Flip-flop JK (Componente 01)
  //   J = 1 liga, K = 1 desliga, J = K = 1 inverte
  //   PRE = forca Q=1
  //   CLR = forca Q=0
  //   Q, Qn = saida e saida invertida
endmodule

module Soma_8_bits (
  input  in_1,
  input  in_2,
  input  in_3,
  input  in_4,
  input  in_5,
  input  in_6,
  input  in_7,
  input  in_8,
  input  in_9,
  input  in_10,
  input  in_11,
  input  in_12,
  input  in_13,
  input  in_14,
  input  in_15,
  input  in_16,
  output out_17,
  output out_18,
  output out_19,
  output out_20,
  output out_21,
  output out_22,
  output out_23,
  output out_24,
  output out_25,
  output out_26,
  output out_27,
  output out_28,
  output out_29,
  output out_30,
  output [7:0] out_31,
  output out_32,
  output out_33
);

  wire and_1_out, and_2_out, and_3_out, and_4_out, and_5_out, and_6_out, and_7_out, and_8_out, and_9_out,
       and_10_out, and_11_out, and_12_out, and_13_out, and_14_out, and_15_out, and_16_out, xor_1_out,
       xor_2_out, xor_3_out, xor_7_out, xor_8_out, xor_9_out, xor_13_out, xor_14_out;

  xor xor_1 (xor_1_out, in_1, in_4);
  and and_1 (and_1_out, in_1, in_4);
  xor xor_2 (xor_2_out, in_7, in_10);
  and and_2 (and_2_out, in_7, in_10);
  xor xor_3 (xor_3_out, in_13, in_15);
  and and_3 (and_3_out, in_13, in_15);
  xor xor_4 (out_17, xor_1_out, 1'b0);
  and and_4 (and_4_out, xor_1_out, 1'b0);
  xor xor_5 (out_23, xor_2_out, out_20);
  and and_5 (and_5_out, xor_2_out, out_20);
  xor xor_6 (out_29, xor_3_out, out_26);
  and and_6 (and_6_out, xor_3_out, out_26);
  or or_1 (out_20, and_4_out, and_1_out);
  or or_2 (out_26, and_5_out, and_2_out);
  or or_3 (out_32, and_6_out, and_3_out);
  xor xor_7 (xor_7_out, in_2, in_5);
  and and_7 (and_7_out, in_2, in_5);
  xor xor_8 (xor_8_out, in_8, in_11);
  and and_8 (and_8_out, in_8, in_11);
  xor xor_9 (xor_9_out, in_14, in_16);
  and and_9 (and_9_out, in_14, in_16);
  xor xor_10 (out_18, xor_7_out, out_27);
  and and_10 (and_10_out, xor_7_out, out_27);
  xor xor_11 (out_24, xor_8_out, out_33);
  and and_11 (and_11_out, xor_8_out, out_33);
  or or_4 (out_21, and_10_out, and_7_out);
  or or_5 (out_27, and_11_out, and_8_out);
  xor xor_12 (out_30, xor_9_out, out_32);
  and and_12 (and_12_out, xor_9_out, out_32);
  or or_6 (out_33, and_12_out, and_9_out);
  xor xor_13 (xor_13_out, in_3, in_6);
  and and_13 (and_13_out, in_3, in_6);
  xor xor_14 (xor_14_out, in_9, in_12);
  and and_14 (and_14_out, in_9, in_12);
  xor xor_15 (out_19, xor_13_out, out_21);
  and and_15 (and_15_out, xor_13_out, out_21);
  xor xor_16 (out_25, xor_14_out, out_22);
  and and_16 (and_16_out, xor_14_out, out_22);
  or or_7 (out_22, and_15_out, and_13_out);
  or or_8 (out_28, and_16_out, and_14_out);

  assign out_31 = {out_25, out_19, out_18, out_24, out_30, out_29, out_23, out_17};

  // Notes on the sheet:
  //   LEGENDA: Soma_8_bits = Somador de 8 bits feito bit a bit (Componente 08)
  //   Entradas: dois numeros de 8 bits
  //   Saida: soma de 8 bits e vai-um
endmodule

module MUX4_1 (
  input  I0,
  input  I1,
  input  I2,
  input  I3,
  input  S1,
  input  S0,
  output Y
);

  wire and_1_out, and_2_out, and_3_out, and_4_out, not_1_out, not_2_out;

  not not_1 (not_1_out, S1);
  not not_2 (not_2_out, S0);
  and and_1 (and_1_out, not_1_out, I0, not_2_out);
  and and_2 (and_2_out, not_1_out, I1, S0);
  and and_3 (and_3_out, S1, I2, not_2_out);
  and and_4 (and_4_out, S1, I3, S0);
  or or_1 (Y, and_1_out, and_2_out, and_3_out, and_4_out);

  // Notes on the sheet:
  //   MUX4_1: Y = I[S1 S0] (1 bit), feito com portas
  //   LEGENDA: MUX4_1 = Multiplexador 4 entradas x 1 bit
  //   I0..I3 = entradas
  //   S1 S0 = seletor
  //   Y = entrada escolhida
endmodule

module MEMORIA_ROM (
  input  [3:0] A,
  output [7:0] D
);

  ROM #(.addrWidth(4)) rom_1 (.addr(A), .data(D));

  // Notes on the sheet:
  //   contents of rom_1 (hex, n*v repeats v):
  //   a0 a1 a2 a3 a4 a5 a6 a7 a8 a9 aa ab ac ad ae af
  //   MEMORIA_ROM: ROM 16x8 (conteudo A0..AF)
  //   LEGENDA: MEMORIA_ROM = Memoria so de leitura, 16 x 8 bits (Componente 05)
  //   A = endereco (4 bits)
  //   D = dado lido (conteudo fixo: 0xA0 + endereco)
endmodule

module MEMORIA_RAM (
  input  [3:0] A,
  input  [7:0] DIN,
  input  CS,
  input  CLK,
  input  WE,
  output [7:0] DOUT
);

  wire and_1_out;

  and and_1 (and_1_out, WE, CS);
  RAM #(.addrWidth(4)) ram_1 (.addr(A), .we(and_1_out), .oe(1'b1), .clk(CLK), .din(DIN), .dout(DOUT));

  // Notes on the sheet:
  //   str = WE . CS
  //   MEMORIA_RAM: RAM 16x8, grava so quando CS=1 e WE=1
  //   LEGENDA: MEMORIA_RAM = Memoria de leitura e escrita, 16 x 8 bits (Componente 06)
  //   A = endereco (4 bits)
  //   DIN = dado a gravar
  //   DOUT = dado lido
  //   CS = Chip Select: so responde quando a regiao 01 esta escolhida
  //   WE = Write Enable (1 = gravar)
  //   CLK = relogio (grava e le na subida)
endmodule

module BANCO_REG (
  input  WA1,
  input  WA0,
  input  WE,
  input  [7:0] WD,
  input  CLK,
  input  R,
  input  RA1_1,
  input  RA1_0,
  input  RA2_1,
  input  RA2_0,
  output [7:0] RD1,
  output [7:0] RD2
);

  wire and_1_out, and_2_out, and_3_out, and_4_out, not_1_out, not_2_out;
  wire [7:0] R0_q, R1_q, R2_q, R3_q;

  not not_1 (not_1_out, WA1);
  not not_2 (not_2_out, WA0);
  and and_1 (and_1_out, not_1_out, not_2_out, WE);
  and and_2 (and_2_out, not_1_out, WA0, WE);
  and and_3 (and_3_out, WA1, not_2_out, WE);
  and and_4 (and_4_out, WA1, WA0, WE);
  Register R0 (.D(WD), .en(and_1_out), .clk(CLK), .Q(R0_q), .clr(R));
  Register R1 (.D(WD), .en(and_2_out), .clk(CLK), .Q(R1_q), .clr(R));
  Register R2 (.D(WD), .en(and_3_out), .clk(CLK), .Q(R2_q), .clr(R));
  Register R3 (.D(WD), .en(and_4_out), .clk(CLK), .Q(R3_q), .clr(R));
  MUX4_8 mux4_8_1 (.I0(R0_q), .I1(R1_q), .I2(R2_q), .I3(R3_q), .S1(RA1_1), .S0(RA1_0), .Y(RD1));
  MUX4_8 mux4_8_2 (.I0(R0_q), .I1(R1_q), .I2(R2_q), .I3(R3_q), .S1(RA2_1), .S0(RA2_0), .Y(RD2));

  // Notes on the sheet:
  //   WA1
  //   WA0
  //   WE
  //   WD
  //   CLK
  //   R
  //   RA1_1
  //   RA1_0
  //   RA2_1
  //   RA2_0
  //   Decodificador 2->4 da escrita: WEk = WE . (WA1 WA0 = k)
  //   BANCO_REG com FIOS DIRETOS (sem tuneis). Cruzamento sem ponto = nao ligado.
  //   WE0
  //   WE1
  //   WE2
  //   WE3
  //   R0
  //   R1
  //   R2
  //   R3
  //   LEGENDA: BANCO_REG = Banco de 4 registradores de 8 bits (Componente 07)
  //   WA1 WA0 = qual registrador GRAVAR (00=R0 ... 11=R3)
  //   WE = habilita a escrita
  //   WD = dado a gravar
  //   CLK = relogio (grava na subida)
  //   R = zera todos
  //   RA1_1 RA1_0 = qual registrador sai em RD1
  //   RA2_1 RA2_0 = qual registrador sai em RD2
  //   RD1, RD2 = dois registradores lidos ao mesmo tempo
  //   MUX4_8 leitura RD1
  //   MUX4_8 leitura RD2
endmodule

module MEMORIA_PARTE1 (
  input  A5,
  input  A4,
  input  [3:0] END,
  input  [7:0] ENTRADA,
  input  ESCREVER,
  input  RELOGIO,
  input  ZERAR,
  output [7:0] SAIDA,
  output ERRO
);

  wire CS_IO, CS_RAM, CS_REG, CS_ROM, ERRO_RAW, not_1_out, not_2_out, P_CALC, P_LIDO, P_W, STR_P, WE_REG;
  wire [7:0] D_RAM, D_REG, D_ROM;

  not not_1 (not_1_out, A5);
  and and_1 (WE_REG, ESCREVER, CS_REG);
  and and_2 (STR_P, ESCREVER, CS_RAM);
  and and_3 (ERRO, ERRO_RAW, CS_RAM);
  not not_2 (not_2_out, A4);
  LED LED_ERRO (.in(ERRO));
  and and_4 (CS_ROM, not_1_out, not_2_out);
  and and_5 (CS_RAM, not_1_out, A4);
  and and_6 (CS_REG, A5, not_2_out);
  and and_7 (CS_IO, A5, A4);
  LED LED_CS_ROM (.in(CS_ROM));
  LED LED_CS_RAM (.in(CS_RAM));
  LED LED_CS_REG (.in(CS_REG));
  LED LED_CS_IO (.in(CS_IO));
  RAM #(.addrWidth(4), .dataWidth(1)) PARIDADE_RAM (
    .addr(END), .we(STR_P), .oe(1'b1), .clk(RELOGIO), .din(P_W), .dout(P_LIDO));
  MEMORIA_ROM memoria_rom_1 (.A(END), .D(D_ROM));
  MEMORIA_RAM memoria_ram_1 (.A(END), .DIN(ENTRADA), .CS(CS_RAM), .CLK(RELOGIO), .WE(ESCREVER), .DOUT(D_RAM));
  BANCO_REG banco_reg_1 (
    .WA1(END[1]), .WA0(END[0]), .WE(WE_REG), .WD(ENTRADA), .CLK(RELOGIO), .R(ZERAR), .RA1_1(END[1]),
    .RA1_0(END[0]), .RA2_1(1'b0), .RA2_0(1'b0), .RD1(D_REG));  // open: RD2
  PARIDADE_IMPAR paridade_impar_1 (.D(ENTRADA), .P(P_W));
  MUX4_8 mux4_8_1 (.I0(D_ROM), .I1(D_RAM), .I2(D_REG), .I3({8{1'b0}}), .S1(A5), .S0(A4), .Y(SAIDA));
  PARIDADE_IMPAR paridade_impar_2 (.D(D_RAM), .P(P_CALC));
  xor2 xor2_1 (.x(P_CALC), .Y(P_LIDO), .S(ERRO_RAW));

  // Other names for the same wires on the sheet: A0 = END[0]; A1 = END[1]

  // Notes on the sheet:
  //   ENTRADAS
  //   END = A3..A0 (4 bits)
  //   SAIDAS
  //   Habilitacoes de escrita e erro
  //   Decodificador 2->4 (A5 A4) -> CS
  //   Regiao de E/S = 00
  //   WE_REG = ESCREVER . CS_REG
  //   STR_P = ESCREVER . CS_RAM
  //   ERRO = (P_calc xor P_lido) . CS_RAM
  //   Distribuidor END -> A0, A1
  //   MEMORIA_ROM
  //   MEMORIA_RAM
  //   BANCO_REG
  //   PARIDADE_IMPAR (escrita)
  //   RAM 16x1 da paridade
  //   MUX4_8 de saida
  //   PARIDADE_IMPAR (leitura)
  //   xor2
  //   LEGENDA: MEMORIA_PARTE1 = Modulo de memoria de 64 bytes
  //   A5 A4 = escolhem o dispositivo: 00=ROM, 01=RAM, 10=Banco de registradores, 11=E/S
  //   END = endereco dentro do dispositivo (A3..A0, 4 bits)
  //   ENTRADA = dado de 8 bits a ser gravado
  //   ESCREVER = 1 para gravar
  //   RELOGIO = grava na subida (0->1)
  //   ZERAR = zera os registradores
  //   SAIDA = dado lido (8 bits)
  //   ERRO = 1 se a paridade falhou (LED)
  //   MUX4_8 = escolhe qual dispositivo vai para SAIDA (seletor = A5 A4)
  //   CS = Chip Select: habilita so o dispositivo escolhido
endmodule

module MEMORIA_PARTE1_FIOS (
  input  A5,
  input  A4,
  input  [3:0] END,
  input  [7:0] ENTRADA,
  input  ESCREVER,
  input  RELOGIO,
  input  ZERAR,
  output [7:0] SAIDA,
  output ERRO
);

  wire and_1_out, and_2_out, and_3_out, and_4_out, and_5_out, and_6_out, not_1_out, not_2_out,
       paridade_impar_1_p, paridade_impar_2_p, PARIDADE_RAM_dout, xor2_1_s;
  wire [7:0] banco_reg_1_rd1, memoria_ram_1_dout, memoria_rom_1_d;

  not not_1 (not_1_out, A5);
  not not_2 (not_2_out, A4);
  and and_1 (and_1_out, ESCREVER, and_5_out);
  and and_2 (and_2_out, ESCREVER, and_4_out);
  and and_3 (and_3_out, not_1_out, not_2_out);
  and and_4 (and_4_out, not_1_out, A4);
  and and_5 (and_5_out, A5, not_2_out);
  and and_6 (and_6_out, A5, A4);
  LED LED_CS_ROM (.in(and_3_out));
  LED LED_CS_RAM (.in(and_4_out));
  LED LED_CS_REG (.in(and_5_out));
  LED LED_CS_IO (.in(and_6_out));
  RAM #(.addrWidth(4), .dataWidth(1)) PARIDADE_RAM (
    .addr(END), .we(and_2_out), .oe(1'b1), .clk(RELOGIO), .din(paridade_impar_1_p), .dout(PARIDADE_RAM_dout));
  MEMORIA_ROM memoria_rom_1 (.A(END), .D(memoria_rom_1_d));
  MEMORIA_RAM memoria_ram_1 (
    .A(END), .DIN(ENTRADA), .CS(and_4_out), .CLK(RELOGIO), .WE(ESCREVER), .DOUT(memoria_ram_1_dout));
  BANCO_REG banco_reg_1 (
    .WA1(END[1]), .WA0(END[0]), .WE(and_1_out), .WD(ENTRADA), .CLK(RELOGIO), .R(ZERAR), .RA1_1(END[1]),
    .RA1_0(END[0]), .RA2_1(1'b0), .RA2_0(1'b0), .RD1(banco_reg_1_rd1));  // open: RD2
  PARIDADE_IMPAR paridade_impar_1 (.D(ENTRADA), .P(paridade_impar_1_p));
  MUX4_8 mux4_8_1 (
    .I0(memoria_rom_1_d), .I1(memoria_ram_1_dout), .I2(banco_reg_1_rd1), .I3({8{1'b0}}), .S1(A5), .S0(A4),
    .Y(SAIDA));
  PARIDADE_IMPAR paridade_impar_2 (.D(memoria_ram_1_dout), .P(paridade_impar_2_p));
  xor2 xor2_1 (.x(paridade_impar_2_p), .Y(PARIDADE_RAM_dout), .S(xor2_1_s));
  and and_7 (ERRO, xor2_1_s, and_4_out);
  LED LED_ERRO (.in(ERRO));

  // Notes on the sheet:
  //   A5
  //   A4
  //   ENTRADA
  //   END
  //   ESCREVER
  //   ZERAR
  //   RELOGIO
  //   Distribuidor: END -> A0 (bit 0), A1 (bit 1)
  //   WE_REG
  //   STR_P
  //   Decodificador A5 A4 -> CS
  //   A0
  //   WE_REG
  //   A1
  //   STR_P
  //   CS_RAM
  //   MEMORIA_PARTE1 com FIOS DIRETOS (sem tuneis). Cruzamento sem ponto = nao ligado.
  //   MEMORIA_ROM
  //   MEMORIA_RAM
  //   BANCO_REG
  //   PARIDADE_IMPAR (escrita)
  //   RAM 16x1 (paridade)
  //   MUX4_8 de saida
  //   PARIDADE_IMPAR (leitura)
  //   LEGENDA: MEMORIA_PARTE1_FIOS = (versao so com fios) Modulo de memoria de 64 bytes
  //   A5 A4 = escolhem o dispositivo: 00=ROM, 01=RAM, 10=Banco de registradores, 11=E/S
  //   END = endereco dentro do dispositivo (A3..A0, 4 bits)
  //   ENTRADA = dado de 8 bits a ser gravado
  //   ESCREVER = 1 para gravar
  //   RELOGIO = grava na subida (0->1)
  //   ZERAR = zera os registradores
  //   SAIDA = dado lido (8 bits)
  //   ERRO = 1 se a paridade falhou (LED)
  //   MUX4_8 = escolhe qual dispositivo vai para SAIDA (seletor = A5 A4)
  //   CS = Chip Select: habilita so o dispositivo escolhido
  //   xor2
endmodule
