// Logisim project parte2_microprogramada.circ as structural Verilog: 14 circuits, main circuit CPU_MICRO
module FF_D (
  input  set,
  input  clock,
  input  data,
  input  reset,
  output Q,
  output Qn
);

  wire nand_1_out, nand_2_out, nand_3_out, nand_4_out, not_1_out, not_2_out;

  not not_1 (not_1_out, set);
  not not_2 (not_2_out, reset);
  nand nand_1 (nand_1_out, not_1_out, nand_4_out, nand_2_out);
  nand nand_2 (nand_2_out, nand_1_out, clock, not_2_out);
  nand nand_3 (nand_3_out, nand_2_out, clock, nand_4_out);
  nand nand_4 (nand_4_out, nand_3_out, data, not_2_out);
  nand nand_5 (Q, not_1_out, nand_2_out, Qn);
  nand nand_6 (Qn, Q, nand_3_out, not_2_out);

  // Notes on the sheet:
  //   LEGENDA: FF_D = Flip-flop D (Componente 01): guarda 1 bit
  //   set = forca Q=1
  //   reset = forca Q=0 (zera)
  //   clock = relogio: grava 'data' na subida (0->1)
  //   data = bit a ser guardado
  //   Q = valor guardado
  //   Qn = Q invertido
endmodule

module DEC_7SEG_S (
  input  A,
  input  B,
  input  C,
  input  D,
  output seg_a,
  output seg_b,
  output seg_c,
  output seg_d,
  output seg_e,
  output seg_f,
  output seg_g
);

  wire and_1_out, and_2_out, and_3_out, and_4_out, and_5_out, and_6_out, and_7_out, and_8_out, and_9_out,
       not_1_out, not_2_out, not_3_out;

  not not_1 (not_1_out, B);
  not not_2 (not_2_out, C);
  not not_3 (not_3_out, D);
  and and_1 (and_1_out, B, D);
  and and_2 (and_2_out, not_1_out, not_3_out);
  and and_3 (and_3_out, not_2_out, not_3_out);
  and and_4 (and_4_out, C, D);
  and and_5 (and_5_out, not_1_out, C);
  and and_6 (and_6_out, C, not_3_out);
  and and_7 (and_7_out, B, not_2_out, D);
  and and_8 (and_8_out, B, not_2_out);
  and and_9 (and_9_out, B, not_3_out);
  or or_1 (seg_a, A, C, and_1_out, and_2_out);
  or or_2 (seg_b, not_1_out, and_3_out, and_4_out);
  or or_3 (seg_c, B, not_2_out, D);
  or or_4 (seg_d, A, and_2_out, and_5_out, and_6_out, and_7_out);
  or or_5 (seg_e, and_2_out, and_6_out);
  or or_6 (seg_f, A, and_3_out, and_8_out, and_9_out);
  or or_7 (seg_g, A, and_5_out, and_8_out, and_6_out);

  // Notes on the sheet:
  //   DEC_7SEG: entrada ABCD (A = MSB), saidas a..g ativas em 1 (0 a 9; 10-15 indiferentes)
  //   LEGENDA: DEC_7SEG = Decodificador de 7 segmentos (Componente 16)
  //   A B C D = numero de 4 bits (A = bit mais alto)
  //   seg_a..seg_g = segmentos acesos no display
endmodule

module MUX4_8 (
  input  [7:0] I0,
  input  [7:0] I1,
  input  [7:0] I2,
  input  [7:0] I3,
  input  S1,
  input  S0,
  output [7:0] Y
);

  wire not_1_out, not_2_out;
  wire [7:0] and_5_out, and_6_out, and_7_out, and_8_out;
  wire [7:7] and_1_out, and_2_out, and_3_out, and_4_out;

  not not_1 (not_1_out, S1);
  not not_2 (not_2_out, S0);
  and and_1 (and_1_out[7], not_1_out, not_2_out);
  and and_2 (and_2_out[7], not_1_out, S0);
  and and_3 (and_3_out[7], S1, not_2_out);
  and and_4 (and_4_out[7], S1, S0);
  assign and_5_out = I0 & {8{and_1_out[7]}};  // AND_Gate and_5, 8 bits wide
  assign and_6_out = I1 & {8{and_2_out[7]}};  // AND_Gate and_6, 8 bits wide
  assign and_7_out = I2 & {8{and_3_out[7]}};  // AND_Gate and_7, 8 bits wide
  assign and_8_out = I3 & {8{and_4_out[7]}};  // AND_Gate and_8, 8 bits wide
  assign Y = and_5_out | and_6_out | and_7_out | and_8_out;  // OR_Gate or_1, 8 bits wide

  // Notes on the sheet:
  //   MUX4_8: Y = I[S1S0]  (S=00->I0, 01->I1, 10->I2, 11->I3)
  //   Decodificacao: e0=S1'S0'  e1=S1'S0  e2=S1S0'  e3=S1S0 ; cada e_k vira mascara de 8 bits no distribuidor
  //   LEGENDA: MUX4_8 = Multiplexador 4 entradas x 8 bits (Componente 02)
  //   I0..I3 = as 4 entradas de 8 bits
  //   S1 S0 = seletor: 00->I0, 01->I1, 10->I2, 11->I3
  //   Y = saida (a entrada escolhida)
endmodule

module BANCO_REG (
  input  WA1,
  input  WA0,
  input  WE,
  input  [7:0] WD,
  input  CLK,
  input  R,
  input  RA1_1,
  input  RA1_0,
  input  RA2_1,
  input  RA2_0,
  output [7:0] RD1,
  output [7:0] RD2
);

  wire and_1_out, and_2_out, and_3_out, and_4_out, not_1_out, not_2_out;
  wire [7:0] R0_q, R1_q, R2_q, R3_q;

  not not_1 (not_1_out, WA1);
  not not_2 (not_2_out, WA0);
  and and_1 (and_1_out, not_1_out, not_2_out, WE);
  and and_2 (and_2_out, not_1_out, WA0, WE);
  and and_3 (and_3_out, WA1, not_2_out, WE);
  and and_4 (and_4_out, WA1, WA0, WE);
  Register R0 (.D(WD), .en(and_1_out), .clk(CLK), .Q(R0_q), .clr(R));
  Register R1 (.D(WD), .en(and_2_out), .clk(CLK), .Q(R1_q), .clr(R));
  Register R2 (.D(WD), .en(and_3_out), .clk(CLK), .Q(R2_q), .clr(R));
  Register R3 (.D(WD), .en(and_4_out), .clk(CLK), .Q(R3_q), .clr(R));
  MUX4_8 mux4_8_1 (.I0(R0_q), .I1(R1_q), .I2(R2_q), .I3(R3_q), .S1(RA1_1), .S0(RA1_0), .Y(RD1));
  MUX4_8 mux4_8_2 (.I0(R0_q), .I1(R1_q), .I2(R2_q), .I3(R3_q), .S1(RA2_1), .S0(RA2_0), .Y(RD2));

  // Notes on the sheet:
  //   WA1
  //   WA0
  //   WE
  //   WD
  //   CLK
  //   R
  //   RA1_1
  //   RA1_0
  //   RA2_1
  //   RA2_0
  //   Decodificador 2->4 da escrita: WEk = WE . (WA1 WA0 = k)
  //   BANCO_REG com FIOS DIRETOS (sem tuneis). Cruzamento sem ponto = nao ligado.
  //   WE0
  //   WE1
  //   WE2
  //   WE3
  //   R0
  //   R1
  //   R2
  //   R3
  //   LEGENDA: BANCO_REG = Banco de 4 registradores de 8 bits (Componente 07)
  //   WA1 WA0 = qual registrador GRAVAR (00=R0 ... 11=R3)
  //   WE = habilita a escrita
  //   WD = dado a gravar
  //   CLK = relogio (grava na subida)
  //   R = zera todos
  //   RA1_1 RA1_0 = qual registrador sai em RD1
  //   RA2_1 RA2_0 = qual registrador sai em RD2
  //   RD1, RD2 = dois registradores lidos ao mesmo tempo
  //   MUX4_8 leitura RD1
  //   MUX4_8 leitura RD2
endmodule

module SOMADOR8 (
  input  [7:0] A,
  input  [7:0] B,
  input  Cin,
  output [7:0] S,
  output Cout
);

  wire and_1_out, and_2_out, and_3_out, and_5_out, and_6_out, and_7_out, and_9_out, and_10_out, and_11_out,
       and_13_out, and_14_out, and_15_out, and_17_out, and_18_out, and_19_out, and_21_out, and_22_out,
       and_23_out, and_25_out, and_26_out, and_27_out, and_29_out, and_30_out, and_31_out, not_1_out,
       not_2_out, not_3_out, not_4_out, not_5_out, not_6_out, not_7_out, not_8_out, not_9_out, not_10_out,
       not_11_out, not_12_out, not_13_out, not_14_out, not_15_out, not_16_out, or_1_out, or_2_out, or_3_out,
       or_4_out, or_5_out, or_6_out, or_7_out, or_8_out, or_9_out, or_10_out, or_11_out, or_12_out,
       or_13_out, or_14_out, or_15_out, or_16_out, or_17_out, or_18_out, or_19_out, or_20_out, or_21_out,
       or_22_out, or_23_out;

  or or_1 (or_1_out, A[0], B[0]);
  and and_1 (and_1_out, A[0], B[0]);
  not not_1 (not_1_out, and_1_out);
  and and_2 (and_2_out, or_1_out, not_1_out);
  or or_2 (or_2_out, and_2_out, Cin);
  and and_3 (and_3_out, and_2_out, Cin);
  not not_2 (not_2_out, and_3_out);
  and and_4 (S[0], or_2_out, not_2_out);
  or or_3 (or_3_out, and_1_out, and_3_out);
  or or_4 (or_4_out, A[1], B[1]);
  and and_5 (and_5_out, A[1], B[1]);
  not not_3 (not_3_out, and_5_out);
  and and_6 (and_6_out, or_4_out, not_3_out);
  or or_5 (or_5_out, and_6_out, or_3_out);
  and and_7 (and_7_out, and_6_out, or_3_out);
  not not_4 (not_4_out, and_7_out);
  and and_8 (S[1], or_5_out, not_4_out);
  or or_6 (or_6_out, and_5_out, and_7_out);
  or or_7 (or_7_out, A[2], B[2]);
  and and_9 (and_9_out, A[2], B[2]);
  not not_5 (not_5_out, and_9_out);
  and and_10 (and_10_out, or_7_out, not_5_out);
  or or_8 (or_8_out, and_10_out, or_6_out);
  and and_11 (and_11_out, and_10_out, or_6_out);
  not not_6 (not_6_out, and_11_out);
  and and_12 (S[2], or_8_out, not_6_out);
  or or_9 (or_9_out, and_9_out, and_11_out);
  or or_10 (or_10_out, A[3], B[3]);
  and and_13 (and_13_out, A[3], B[3]);
  not not_7 (not_7_out, and_13_out);
  and and_14 (and_14_out, or_10_out, not_7_out);
  or or_11 (or_11_out, and_14_out, or_9_out);
  and and_15 (and_15_out, and_14_out, or_9_out);
  not not_8 (not_8_out, and_15_out);
  and and_16 (S[3], or_11_out, not_8_out);
  or or_12 (or_12_out, and_13_out, and_15_out);
  or or_13 (or_13_out, A[4], B[4]);
  and and_17 (and_17_out, A[4], B[4]);
  not not_9 (not_9_out, and_17_out);
  and and_18 (and_18_out, or_13_out, not_9_out);
  or or_14 (or_14_out, and_18_out, or_12_out);
  and and_19 (and_19_out, and_18_out, or_12_out);
  not not_10 (not_10_out, and_19_out);
  and and_20 (S[4], or_14_out, not_10_out);
  or or_15 (or_15_out, and_17_out, and_19_out);
  or or_16 (or_16_out, A[5], B[5]);
  and and_21 (and_21_out, A[5], B[5]);
  not not_11 (not_11_out, and_21_out);
  and and_22 (and_22_out, or_16_out, not_11_out);
  or or_17 (or_17_out, and_22_out, or_15_out);
  and and_23 (and_23_out, and_22_out, or_15_out);
  not not_12 (not_12_out, and_23_out);
  and and_24 (S[5], or_17_out, not_12_out);
  or or_18 (or_18_out, and_21_out, and_23_out);
  or or_19 (or_19_out, A[6], B[6]);
  and and_25 (and_25_out, A[6], B[6]);
  not not_13 (not_13_out, and_25_out);
  and and_26 (and_26_out, or_19_out, not_13_out);
  or or_20 (or_20_out, and_26_out, or_18_out);
  and and_27 (and_27_out, and_26_out, or_18_out);
  not not_14 (not_14_out, and_27_out);
  and and_28 (S[6], or_20_out, not_14_out);
  or or_21 (or_21_out, and_25_out, and_27_out);
  or or_22 (or_22_out, A[7], B[7]);
  and and_29 (and_29_out, A[7], B[7]);
  not not_15 (not_15_out, and_29_out);
  and and_30 (and_30_out, or_22_out, not_15_out);
  or or_23 (or_23_out, and_30_out, or_21_out);
  and and_31 (and_31_out, and_30_out, or_21_out);
  not not_16 (not_16_out, and_31_out);
  and and_32 (S[7], or_23_out, not_16_out);
  or or_24 (Cout, and_29_out, and_31_out);

  // Notes on the sheet:
  //   SOMADOR8: S = A + B + Cin (8 somadores completos em cascata, XOR feito com AND/OR/NOT)
  //   LEGENDA: SOMADOR8 = Somador de 8 bits (Componente 08)
  //   A, B = numeros de 8 bits
  //   Cin = vai-um de entrada
  //   S = A + B + Cin
  //   Cout = vai-um de saida
endmodule

module somador1bit_04 (
  input  Cin,
  input  A,
  input  B,
  output S,
  output Cout
);

  wire and_1_out, and_2_out, and_3_out, xor_1_out;

  xor xor_1 (xor_1_out, A, B);
  and and_1 (and_1_out, A, B);
  and and_2 (and_2_out, B, Cin);
  and and_3 (and_3_out, A, Cin);
  xor xor_2 (S, xor_1_out, Cin);
  or or_1 (Cout, and_1_out, and_2_out, and_3_out);
endmodule

module SOMA_MAIS_4 (
  input  [7:0] entrada,
  output [7:0] saida
);

  wire not_1_out, somador1bit_04_1_cout, somador1bit_04_2_cout, somador1bit_04_3_cout, somador1bit_04_4_cout,
       somador1bit_04_5_cout, somador1bit_04_6_cout, somador1bit_04_7_cout;

  somador1bit_04 somador1bit_04_1 (.A(entrada[0]), .B(1'b0), .Cin(1'b0), .S(saida[0]), .Cout(somador1bit_04_1_cout));
  somador1bit_04 somador1bit_04_2 (
    .A(entrada[1]), .B(1'b0), .Cin(somador1bit_04_1_cout), .S(saida[1]), .Cout(somador1bit_04_2_cout));
  somador1bit_04 somador1bit_04_3 (
    .A(entrada[2]), .B(not_1_out), .Cin(somador1bit_04_2_cout), .S(saida[2]), .Cout(somador1bit_04_3_cout));
  not not_1 (not_1_out, 1'b0);
  somador1bit_04 somador1bit_04_4 (
    .A(entrada[3]), .B(1'b0), .Cin(somador1bit_04_3_cout), .S(saida[3]), .Cout(somador1bit_04_4_cout));
  somador1bit_04 somador1bit_04_5 (
    .A(entrada[4]), .B(1'b0), .Cin(somador1bit_04_4_cout), .S(saida[4]), .Cout(somador1bit_04_5_cout));
  somador1bit_04 somador1bit_04_6 (
    .A(entrada[5]), .B(1'b0), .Cin(somador1bit_04_5_cout), .S(saida[5]), .Cout(somador1bit_04_6_cout));
  somador1bit_04 somador1bit_04_7 (
    .A(entrada[6]), .B(1'b0), .Cin(somador1bit_04_6_cout), .S(saida[6]), .Cout(somador1bit_04_7_cout));
  somador1bit_04 somador1bit_04_8 (.A(entrada[7]), .B(1'b0), .Cin(somador1bit_04_7_cout), .S(saida[7]));  // open: Cout

  // Notes on the sheet:
  //   LEGENDA: SOMA_MAIS_4 = Somador de 8 bits com constante 4 (Componente 04)
  //   entrada = numero de 8 bits (PC)
  //   saida = entrada + 4
endmodule

module EXT_SINAL_4_8 (
  input  A3,
  input  A2,
  input  A1,
  input  A0,
  output [7:0] EXT
);


  assign EXT = {{5{A3}}, A2, A1, A0};

  // Notes on the sheet:
  //   A3 = bit de sinal: copiado para os bits 3 a 7 (sem portas logicas)
  //   LEGENDA: EXT_SINAL_4_8 = Extensor de sinal 4 -> 8 bits (Componente 11)
  //   A3..A0 = imediato de 4 bits (A3 = sinal)
  //   EXT = mesmo numero em 8 bits (A3 copiado nos bits 4 a 7)
endmodule

module ULA8 (
  input  [7:0] A,
  input  [7:0] B,
  input  OP1,
  input  OP0,
  output [7:0] RES,
  output ZERO_ULA
);

  wire and_1_out, not_1_out, or_2_out, or_3_out, or_4_out;
  wire [7:0] and_2_out, mux4_8_1_y, not_2_out, or_1_out, somador8_1_s;

  not not_1 (not_1_out, OP1);
  and and_1 (and_1_out, not_1_out, OP0);
  assign not_2_out = ~B;  // NOT_Gate not_2, 8 bits wide
  assign and_2_out = A & B;  // AND_Gate and_2, 8 bits wide
  assign or_1_out = A | B;  // OR_Gate or_1, 8 bits wide
  or or_2 (or_2_out, RES[0], RES[1], RES[2], RES[3]);
  MUX4_8 mux4_8_1 (.I0(B), .I1(not_2_out), .I2(B), .I3(B), .S1(OP1), .S0(OP0), .Y(mux4_8_1_y));
  SOMADOR8 somador8_1 (.A(A), .B(mux4_8_1_y), .Cin(and_1_out), .S(somador8_1_s));  // open: Cout
  MUX4_8 mux4_8_2 (.I0(somador8_1_s), .I1(somador8_1_s), .I2(and_2_out), .I3(or_1_out), .S1(OP1), .S0(OP0), .Y(RES));
  not not_3 (ZERO_ULA, or_3_out);
  or or_3 (or_3_out, or_2_out, or_4_out);
  or or_4 (or_4_out, RES[4], RES[5], RES[6], RES[7]);

  // Notes on the sheet:
  //   SUBT = OP1'.OP0 (subtracao: inverte B e Cin = 1)
  //   ZERO_ULA = NOT(r7+...+r0)
  //   MUX4_8: B ou NOT B
  //   SOMADOR8 (Componente 08): A + BX + Cin
  //   MUX4_8: 00 soma | 01 sub | 10 AND | 11 OR
  //   ULA8 com FIOS DIRETOS (sem tuneis). Cruzamento sem ponto = nao ligado.
  //   LEGENDA: ULA8 = Unidade Logica e Aritmetica de 8 bits (Componente 10)
  //   A, B = operandos
  //   OP1 OP0 = 00 soma, 01 subtracao, 10 AND, 11 OR
  //   RES = resultado
  //   ZERO_ULA = 1 se RES = 0
  //   SUBT = subtracao: inverte B e soma 1 (complemento de 2)
endmodule

module CONTROLE_ULA (
  input  ALUOp1,
  input  ALUOp0,
  input  F1,
  input  F0,
  output ULA_OP1,
  output ULA_OP0
);

  wire and_2_out, and_3_out, not_1_out;

  not not_1 (not_1_out, ALUOp1);
  // NOT_Gate not_2 has open pins: in=ALUOp0, out=open
  // NOT_Gate not_3 has open pins: in=F1, out=open
  // NOT_Gate not_4 has open pins: in=F0, out=open
  and and_1 (ULA_OP1, ALUOp1, F1);
  and and_2 (and_2_out, ALUOp1, F0);
  and and_3 (and_3_out, not_1_out, ALUOp0);
  or or_1 (ULA_OP0, and_2_out, and_3_out);

  // Notes on the sheet:
  //   CONTROLE_ULA com FIOS DIRETOS (sem tuneis). Cruzamento sem ponto = nao ligado.
  //   LEGENDA: CONTROLE_ULA = Escolhe a operacao da ULA
  //   ALUOp = 00 soma, 01 subtracao, 10 operacao dada pelo funct
  //   F1 F0 = funct da instrucao (00 add, 01 sub, 10 and, 11 or)
  //   ULA_OP1 ULA_OP0 = operacao enviada a ULA
endmodule

module CAMINHO_DADOS (
  input  CLK,
  input  R,
  input  ZERAR_REG,
  input  CARGA,
  input  CREG1,
  input  CREG0,
  input  [7:0] CDADO,
  input  PCWrite,
  input  PCWriteCond,
  input  PCSource,
  input  MemRead,
  input  IRWrite,
  input  RegWrite,
  input  ALUSrcA,
  input  ALUSrcB1,
  input  ALUSrcB0,
  input  ALUOp1,
  input  ALUOp0,
  output BEQ,
  output [7:0] PC,
  output [7:0] IR,
  output [7:0] RD1,
  output [7:0] REG_A,
  output [7:0] REG_B,
  output [7:0] ULA,
  output [7:0] ULAOUT,
  output ZERO_ULA,
  output [7:0] PC4
);

  wire and_1_out, and_2_out, and_4_out, and_5_out, and_6_out, and_7_out, controle_ula_1_ula_op0,
       controle_ula_1_ula_op1, not_1_out, not_2_out, or_1_out, or_2_out, or_3_out, or_4_out;
  wire [7:0] banco_reg_1_rd2, ext_sinal_4_8_1_ext, mux4_8_1_y, mux4_8_2_y, mux4_8_3_y, mux4_8_4_y, rom_1_data;

  Register #(.width(8)) u_PC (.D(mux4_8_1_y), .en(or_1_out), .clk(CLK), .Q(PC), .clr(R));
  and and_1 (and_1_out, PCWriteCond, ZERO_ULA);
  or or_1 (or_1_out, PCWrite, and_1_out);
  MUX4_8 mux4_8_1 (.I0(ULA), .I1(ULAOUT), .I2(ULA), .I3(ULAOUT), .S1(1'b0), .S0(PCSource), .Y(mux4_8_1_y));
  SOMA_MAIS_4 soma_mais_4_1 (.entrada(PC), .saida(PC4));
  ROM #(.addrWidth(4), .dataWidth(8)) rom_1 (.addr(PC[5:2]), .data(rom_1_data));
  Register #(.width(8)) u_IR (.D(rom_1_data), .en(and_2_out), .clk(CLK), .Q(IR), .clr(R));
  not not_1 (not_1_out, IR[7]);
  and and_2 (and_2_out, IRWrite, MemRead);
  and and_3 (BEQ, not_1_out, IR[6]);
  or or_2 (or_2_out, CARGA, RegWrite);
  Register #(.width(8)) A (.D(RD1), .en(1'b1), .clk(CLK), .Q(REG_A), .clr(R));
  EXT_SINAL_4_8 ext_sinal_4_8_1 (.A3(IR[3]), .A2(IR[2]), .A1(IR[1]), .A0(IR[0]), .EXT(ext_sinal_4_8_1_ext));
  MUX4_8 mux4_8_2 (.I0(ULAOUT), .I1(CDADO), .I2(ULAOUT), .I3(CDADO), .S1(1'b0), .S0(CARGA), .Y(mux4_8_2_y));
  not not_2 (not_2_out, CARGA);
  // NOT_Gate not_3 has open pins: in=CREG1, out=open
  // NOT_Gate not_4 has open pins: in=CREG0, out=open
  // NOT_Gate not_5 has open pins: in=IR[5], out=open
  // NOT_Gate not_6 has open pins: in=IR[4], out=open
  Register #(.width(8)) B (.D(banco_reg_1_rd2), .en(1'b1), .clk(CLK), .Q(REG_B), .clr(R));
  and and_4 (and_4_out, CARGA, CREG1);
  BANCO_REG banco_reg_1 (
    .WA1(or_3_out), .WA0(or_4_out), .WE(or_2_out), .WD(mux4_8_2_y), .CLK(CLK), .R(ZERAR_REG),
    .RA1_1(or_3_out), .RA1_0(or_4_out), .RA2_1(IR[3]), .RA2_0(IR[2]), .RD1(RD1), .RD2(banco_reg_1_rd2));
  and and_5 (and_5_out, not_2_out, IR[5]);
  and and_6 (and_6_out, CARGA, CREG0);
  and and_7 (and_7_out, not_2_out, IR[4]);
  or or_3 (or_3_out, and_4_out, and_5_out);
  or or_4 (or_4_out, and_6_out, and_7_out);
  MUX4_8 mux4_8_3 (.I0(PC), .I1(REG_A), .I2(PC), .I3(REG_A), .S1(1'b0), .S0(ALUSrcA), .Y(mux4_8_3_y));
  CONTROLE_ULA controle_ula_1 (
    .ALUOp1(ALUOp1), .ALUOp0(ALUOp0), .F1(IR[1]), .F0(IR[0]), .ULA_OP1(controle_ula_1_ula_op1),
    .ULA_OP0(controle_ula_1_ula_op0));
  Register #(.width(8)) u_ULAOut (.D(ULA), .en(1'b1), .clk(CLK), .Q(ULAOUT), .clr(R));
  MUX4_8 mux4_8_4 (
    .I0(REG_B), .I1(8'h4), .I2({ext_sinal_4_8_1_ext[5:0], 2'b00}), .I3({8{1'b0}}), .S1(ALUSrcB1),
    .S0(ALUSrcB0), .Y(mux4_8_4_y));
  ULA8 ula8_1 (
    .A(mux4_8_3_y), .B(mux4_8_4_y), .OP1(controle_ula_1_ula_op1), .OP0(controle_ula_1_ula_op0), .RES(ULA),
    .ZERO_ULA(ZERO_ULA));

  // Notes on the sheet:
  //   PC
  //   MUX PCSource: 0 ULA, 1 ULAOut
  //   Somador +4 (Componente 04): PC4 = PC + 4
  //   PCEN = PCWrite + PCWriteCond.Zero
  //   CAMINHO_DADOS com FIOS DIRETOS (sem tuneis). Cruzamento sem ponto = nao ligado.
  //   IR: [7:6] opcode (00 R, 01 beq) | [5:4] rs=rd | [3:2] rt | [1:0] funct | imm = IR[3:0]
  //   Modo CARGA (inicializar/ler registradores): endereco = CREG, dado = CDADO
  //   contents of rom_1 (hex, n*v repeats v):
  //   18 71 14 51 19 1a 1b 4f 0 0 0 0 0 0 0 0
  //   IR
  //   ROM de programa 16x8 (Componente 05), endereco = PC[5:2]
  //   LEGENDA: CAMINHO_DADOS = PC, ROM, IR, banco, A, B, ULA e ULAOut
  //   PC = Contador de Programa
  //   ROM = memoria de programa (endereco = PC[5:2])
  //   IR = Registrador de Instrucao: [7:6] opcode [5:4] rs=rd [3:2] rt [1:0] funct
  //   BANCO_REG = R0..R3
  //   A, B = operandos lidos
  //   ULAOut = resultado guardado
  //   PCWrite / PCWriteCond = escrever o PC (sempre / so se ZERO)
  //   PCSource = origem do novo PC: 0 ULA, 1 ULAOut
  //   MemRead = ler a ROM
  //   IRWrite = carregar o IR
  //   RegWrite = gravar em rd
  //   ALUSrcA = 1a entrada da ULA: 0 PC, 1 A
  //   ALUSrcB1 B0 = 2a entrada: 00 B, 01 constante 4, 10 ext(imm)<<2
  //   ALUOp1 ALUOp0 = 00 soma, 01 subtracao, 10 usa o funct
  //   EXT = extensor de sinal 4->8
  //   PC4 = PC + 4 (somador, Componente 04)
  //   CARGA, CREG, CDADO = inicializar registradores
  //   ZERO_ULA = resultado = 0
  //   EXT2 = ext(imm) << 2
  //   A
  //   Extensor de sinal 4->8 (Componente 11)
  //   B
  //   BANCO_REG (Componente 07): 4 x 8 bits, R1 = rs (ou CREG), R2 = rt, escrita em rd = rs
  //   MUX ALUSrcA: 0 PC, 1 A
  //   ULAOut
  //   MUX ALUSrcB (Componente 02): 00 B, 01 4, 10 ext<<2
  //   ULA8 (Componente 10)
endmodule

module CONTADOR_UPC (
  input  LD,
  input  D2,
  input  D1,
  input  D0,
  input  CLK,
  input  R,
  output Q2,
  output Q1,
  output Q0
);

  wire and_1_out, and_2_out, and_3_out, and_4_out, and_5_out, and_6_out, and_7_out, and_8_out, and_9_out,
       not_1_out, not_5_out, not_6_out, not_7_out, or_1_out, or_2_out, or_3_out;

  not not_1 (not_1_out, LD);
  // NOT_Gate not_2 has open pins: in=D2, out=open
  // NOT_Gate not_3 has open pins: in=D1, out=open
  // NOT_Gate not_4 has open pins: in=D0, out=open
  not not_5 (not_5_out, Q2);
  not not_6 (not_6_out, Q1);
  not not_7 (not_7_out, Q0);
  FF_D ff_d_1 (.set(1'b0), .clock(CLK), .data(or_1_out), .reset(R), .Q(Q0));  // open: Qn
  FF_D ff_d_2 (.set(1'b0), .clock(CLK), .data(or_2_out), .reset(R), .Q(Q1));  // open: Qn
  FF_D ff_d_3 (.set(1'b0), .clock(CLK), .data(or_3_out), .reset(R), .Q(Q2));  // open: Qn
  and and_1 (and_1_out, LD, D0);
  and and_2 (and_2_out, not_1_out, not_7_out);
  and and_3 (and_3_out, LD, D1);
  and and_4 (and_4_out, not_1_out, Q1, not_7_out);
  and and_5 (and_5_out, not_1_out, not_6_out, Q0);
  and and_6 (and_6_out, LD, D2);
  and and_7 (and_7_out, not_1_out, Q2, not_6_out);
  and and_8 (and_8_out, not_1_out, Q2, not_7_out);
  and and_9 (and_9_out, not_1_out, not_5_out, Q1, Q0);
  or or_1 (or_1_out, and_1_out, and_2_out);
  or or_2 (or_2_out, and_3_out, and_4_out, and_5_out);
  or or_3 (or_3_out, and_6_out, and_7_out, and_8_out, and_9_out);

  // Notes on the sheet:
  //   LEGENDA: CONTADOR_UPC = Contador sincrono de 3 bits com carga (Componente 13)
  //   LD = 1 carrega D2 D1 D0, LD = 0 conta (+1), R = zera
  //   Q2 Q1 Q0 = valor do contador (endereco da ROM de microcodigo)
  //   FF D -> Q0
  //   FF D -> Q1
  //   FF D -> Q2
  //   CONTADOR_UPC com FIOS DIRETOS (sem tuneis). Cruzamento sem ponto = nao ligado.
endmodule

module UC_MICRO (
  input  CLK,
  input  R,
  input  B,
  output Q2,
  output Q1,
  output Q0,
  output PCWrite,
  output PCWriteCond,
  output PCSource,
  output MemRead,
  output IRWrite,
  output RegWrite,
  output ALUSrcA,
  output ALUSrcB1,
  output ALUSrcB0,
  output ALUOp1,
  output ALUOp0
);

  wire and_1_out, and_2_out, dec_7seg_s_1_seg_a, dec_7seg_s_1_seg_b, dec_7seg_s_1_seg_c, dec_7seg_s_1_seg_d,
       dec_7seg_s_1_seg_e, dec_7seg_s_1_seg_f, dec_7seg_s_1_seg_g, not_2_out, not_3_out, not_4_out,
       not_5_out, not_6_out, not_7_out, or_1_out;
  wire [3:0] MICROCODIGO_data;

  ROM #(.addrWidth(3), .dataWidth(8)) MICROCODIGO (
    .addr({Q2, Q1, Q0}), .data({ALUOp1, ALUOp0, ALUSrcB1, ALUSrcA, MICROCODIGO_data}));
  // NOT_Gate not_1 has open pins: in=MICROCODIGO_data[1], out=open
  not not_2 (not_2_out, MICROCODIGO_data[0]);
  not not_3 (not_3_out, B);
  not not_4 (not_4_out, ALUSrcB1);
  CONTADOR_UPC contador_upc_1 (
    .LD(or_1_out), .D2(and_1_out), .D1(and_2_out), .D0(1'b0), .CLK(CLK), .R(R), .Q2(Q2), .Q1(Q1), .Q0(Q0));
  not not_5 (not_5_out, ALUSrcA);
  not not_6 (not_6_out, MICROCODIGO_data[3]);
  not not_7 (not_7_out, MICROCODIGO_data[2]);
  and and_1 (and_1_out, MICROCODIGO_data[1], not_2_out, B);
  and and_2 (and_2_out, MICROCODIGO_data[1], not_2_out, not_3_out);
  and and_3 (ALUSrcB0, not_4_out, not_5_out);
  and and_4 (IRWrite, not_6_out, MICROCODIGO_data[2]);
  _7_Segment_Display u_7_segment_display_1 (
    .g(dec_7seg_s_1_seg_g), .f(dec_7seg_s_1_seg_f), .a(dec_7seg_s_1_seg_a), .b(dec_7seg_s_1_seg_b),
    .e(dec_7seg_s_1_seg_e), .d(dec_7seg_s_1_seg_d), .c(dec_7seg_s_1_seg_c));  // open: dp
  and and_5 (RegWrite, MICROCODIGO_data[3], not_7_out);
  and and_6 (PCSource, MICROCODIGO_data[3], MICROCODIGO_data[2]);
  or or_1 (or_1_out, MICROCODIGO_data[1], MICROCODIGO_data[0]);
  DEC_7SEG_S dec_7seg_s_1 (
    .A(1'b0), .B(Q2), .C(Q1), .D(Q0), .seg_a(dec_7seg_s_1_seg_a), .seg_b(dec_7seg_s_1_seg_b),
    .seg_c(dec_7seg_s_1_seg_c), .seg_d(dec_7seg_s_1_seg_d), .seg_e(dec_7seg_s_1_seg_e),
    .seg_f(dec_7seg_s_1_seg_f), .seg_g(dec_7seg_s_1_seg_g));

  assign MemRead = IRWrite;
  assign PCWrite = ALUSrcB0;
  assign PCWriteCond = PCSource;

  // Notes on the sheet:
  //   LEGENDA: UC_MICRO = Unidade de controle microprogramada
  //   CLK = relogio
  //   R = reset
  //   B = 1 se a instrucao e beq
  //   uPC = microcontador de programa (CONTADOR_UPC, 3 bits)
  //   ROM = microcodigo 04 22 90 99 5D
  //   Microinstrucao: ULAOp (7..6), Fonte (5..4), Acao (3..2), Seq (1..0)
  //   Seq: 00 proxima, 01 volta a busca, 10 despacho (beq->4, tipo R->2)
  //   LD = carregar o uPC (desvio)
  //   Q2 Q1 Q0 = endereco atual da microinstrucao
  //   Seq: 00 conta | 01,11 carrega 000 | 10 despacho: carrega 100 (beq) ou 010 (tipo R)
  //   contents of MICROCODIGO (hex, n*v repeats v):
  //   4 22 90 99 5d 0 0 0
  //   bits 7..6 ULAOp | 5..4 Fonte | 3..2 Acao | 1..0 Seq
  //   uPC: CONTADOR_UPC (Componente 13)
  //   ROM 8x8 (Componente 05): 04 22 90 99 5D
  //   UC_MICRO com FIOS DIRETOS (sem tuneis). Cruzamento sem ponto = nao ligado.
  //   ESTADO
endmodule

module CPU_MICRO (
  input  CLK,
  input  R,
  input  ZERAR_REG,
  input  CARGA,
  input  CREG1,
  input  CREG0,
  input  [7:0] CDADO,
  output Q2,
  output Q1,
  output Q0,
  output [7:0] PC,
  output [7:0] IR,
  output [7:0] RD1,
  output [7:0] ULAOUT,
  output ZERO_ULA,
  output [7:0] REG_A,
  output [7:0] REG_B,
  output [7:0] PC4,
  output IRWrite,
  output PCWrite,
  output PCWriteCond,
  output RegWrite,
  output BEQ
);

  wire dec_7seg_s_1_seg_a, dec_7seg_s_1_seg_b, dec_7seg_s_1_seg_c, dec_7seg_s_1_seg_d, dec_7seg_s_1_seg_e,
       dec_7seg_s_1_seg_f, dec_7seg_s_1_seg_g, uc_micro_1_aluop0, uc_micro_1_aluop1, uc_micro_1_alusrca,
       uc_micro_1_alusrcb0, uc_micro_1_alusrcb1, uc_micro_1_memread, uc_micro_1_pcsource;

  _7_Segment_Display u_7_segment_display_1 (
    .g(dec_7seg_s_1_seg_g), .f(dec_7seg_s_1_seg_f), .a(dec_7seg_s_1_seg_a), .b(dec_7seg_s_1_seg_b),
    .e(dec_7seg_s_1_seg_e), .d(dec_7seg_s_1_seg_d), .c(dec_7seg_s_1_seg_c));  // open: dp
  UC_MICRO uc_micro_1 (
    .CLK(CLK), .R(R), .B(BEQ), .Q2(Q2), .Q1(Q1), .Q0(Q0), .PCWrite(PCWrite), .PCWriteCond(PCWriteCond),
    .PCSource(uc_micro_1_pcsource), .MemRead(uc_micro_1_memread), .IRWrite(IRWrite), .RegWrite(RegWrite),
    .ALUSrcA(uc_micro_1_alusrca), .ALUSrcB1(uc_micro_1_alusrcb1), .ALUSrcB0(uc_micro_1_alusrcb0),
    .ALUOp1(uc_micro_1_aluop1), .ALUOp0(uc_micro_1_aluop0));
  CAMINHO_DADOS caminho_dados_1 (
    .CLK(CLK), .R(R), .ZERAR_REG(ZERAR_REG), .CARGA(CARGA), .CREG1(CREG1), .CREG0(CREG0), .CDADO(CDADO),
    .PCWrite(PCWrite), .PCWriteCond(PCWriteCond), .PCSource(uc_micro_1_pcsource),
    .MemRead(uc_micro_1_memread), .IRWrite(IRWrite), .RegWrite(RegWrite), .ALUSrcA(uc_micro_1_alusrca),
    .ALUSrcB1(uc_micro_1_alusrcb1), .ALUSrcB0(uc_micro_1_alusrcb0), .ALUOp1(uc_micro_1_aluop1),
    .ALUOp0(uc_micro_1_aluop0), .BEQ(BEQ), .PC(PC), .IR(IR), .RD1(RD1), .REG_A(REG_A), .REG_B(REG_B),
    .ULAOUT(ULAOUT), .ZERO_ULA(ZERO_ULA), .PC4(PC4));  // open: ULA
  DEC_7SEG_S dec_7seg_s_1 (
    .A(1'b0), .B(Q2), .C(Q1), .D(Q0), .seg_a(dec_7seg_s_1_seg_a), .seg_b(dec_7seg_s_1_seg_b),
    .seg_c(dec_7seg_s_1_seg_c), .seg_d(dec_7seg_s_1_seg_d), .seg_e(dec_7seg_s_1_seg_e),
    .seg_f(dec_7seg_s_1_seg_f), .seg_g(dec_7seg_s_1_seg_g));

  // Notes on the sheet:
  //   LEGENDA: CPU multiciclo 8 bits (UC MICROPROGRAMADA + caminho
  //   de dados)
  //   CLK = relogio (1 pulso = 1 ciclo)
  //   R = reset (volta ao estado 0, PC = 0)
  //   ZERAR_REG = zera R0..R3
  //   CARGA = 1 modo de carga dos registradores
  //   CREG1 CREG0 = registrador da carga (01=R1, 10=R2)
  //   CDADO = valor da carga
  //   Q2 Q1 Q0 = estado da UC (S0 busca, S1 decod., S2 exec. R, S3
  //      concl. R, S4 beq)
  //   PC = Contador de Programa (endereco da instrucao)
  //   PC4 = PC + 4
  //   IR = Registrador de Instrucao (instrucao atual)
  //   RD1 = valor do registrador rs
  //   REG_A, REG_B = operandos da ULA
  //   ULAOUT = resultado guardado da ULA
  //   ZERO_ULA = 1 se resultado = 0
  //   IRWrite = carrega o IR
  //   PCWrite = escreve o PC
  //   PCWriteCond = escreve o PC se ZERO (beq)
  //   RegWrite = grava no registrador
  //   BEQ = 1 se a instrucao no IR e beq (opcode 01)
  //   ESTADO
  //   UC_MICRO
  //   CAMINHO_DADOS
  //   CPU_MICRO com FIOS DIRETOS (sem tuneis). Cruzamento sem ponto = nao ligado.
endmodule
